// Logisim project Tetris.circ as structural Verilog: 17 circuits, main circuit Xdecoder
module main (
  input  Frequency128Hz
);

  wire Clear, clock_1_out, Down, Down_OK, FastClock, GameOver, GMClock, Left, Left_OK, Lock, Reset, Right,
       Right_OK, Rotate, Rotate_OK, SlowClock;
  wire [2:0] Random_Block;
  wire [3:0] AddScore, Block_X, LV, Next_Length, Seg_1, Seg_10, XY_length;
  wire [4:0] Block_Y;
  wire [9:0] NewRow0, NewRow1, NewRow2, NewRow3, NewRow4, NewRow5, NewRow6, NewRow7, NewRow8, NewRow9,
       NewRow10, NewRow11, NewRow12, NewRow13, NewRow14, NewRow15, NewRow16, NewRow17, NewRow18, NewRow19,
       Overlay_Out0, Overlay_Out1, Overlay_Out2, Overlay_Out3, Overlay_Out4, Overlay_Out5, Overlay_Out6,
       Overlay_Out7, Overlay_Out8, Overlay_Out9, Overlay_Out10, Overlay_Out11, Overlay_Out12, Overlay_Out13,
       Overlay_Out14, Overlay_Out15, Overlay_Out16, Overlay_Out17, Overlay_Out18, Overlay_Out19, Row0, Row1,
       Row2, Row3, Row4, Row5, Row6, Row7, Row8, Row9, Row10, Row11, Row12, Row13, Row14, Row15, Row16,
       Row17, Row18, Row19;
  wire [15:0] Next_Rotate, Shape_out;

  DotMatrix #(.inputtype("row"), .matrixcols(10), .matrixrows(20)) dotmatrix_1 (
    .row0(Overlay_Out0), .row1(Overlay_Out1), .row2(Overlay_Out2), .row3(Overlay_Out3), .row4(Overlay_Out4),
    .row5(Overlay_Out5), .row6(Overlay_Out6), .row7(Overlay_Out7), .row8(Overlay_Out8), .row9(Overlay_Out9),
    .row10(Overlay_Out10), .row11(Overlay_Out11), .row12(Overlay_Out12), .row13(Overlay_Out13),
    .row14(Overlay_Out14), .row15(Overlay_Out15), .row16(Overlay_Out16), .row17(Overlay_Out17),
    .row18(Overlay_Out18), .row19(Overlay_Out19));
  Hex_Digit_Display Score (.value(Seg_1));  // open: dp
  Hex_Digit_Display hex_digit_display_1 (.value(Seg_10));  // open: dp
  Button u_Left (.out(Left));
  Button u_Right (.out(Right));
  Button u_Down (.out(Down));
  Hex_Digit_Display Level (.value(LV));  // open: dp
  LED u_GameOver (.in(GameOver));
  LED u_Clear (.in(Clear));
  Button u_Rotate (.out(Rotate));
  Block_Random_Generator block_random_generator_1 (.Lock(Lock), .SlowClock(SlowClock), .Random_Block(Random_Block));
  Score_Level score_level_1 (
    .AddScore(AddScore), .Lock(Lock), .Seg_1(Seg_1), .Seg_10(Seg_10), .LV(LV), .Clear(Clear));  // open: Score
  Collision_Detector collision_detector_1 (
    .Shape_out(Shape_out), .Next_Rotate(Next_Rotate), .Block_X(Block_X), .Block_Y(Block_Y),
    .XYlength(XY_length), .Next_Length(Next_Length), .Row0(Row0), .Row1(Row1), .Row2(Row2), .Row3(Row3),
    .Row4(Row4), .Row5(Row5), .Row6(Row6), .Row7(Row7), .Row8(Row8), .Row9(Row9), .Row10(Row10),
    .Row11(Row11), .Row12(Row12), .Row13(Row13), .Row14(Row14), .Row15(Row15), .Row16(Row16), .Row17(Row17),
    .Row18(Row18), .Row19(Row19), .Right_OK(Right_OK), .Left_OK(Left_OK), .Down_OK(Down_OK),
    .Rotate_OK(Rotate_OK));
  Block_Control block_control_1 (
    .Left(Left), .Left_OK(Left_OK), .Right(Right), .Right_OK(Right_OK), .Down(Down), .Down_OK(Down_OK),
    .FastClock(FastClock), .SlowClock(SlowClock), .X_out(Block_X), .Y_out(Block_Y), .Reset(Reset),
    .GMClock(GMClock), .Lock(Lock), .GameOver(GameOver));
  GameMemory gamememory_1 (
    .Clock(GMClock), .Lock(Lock), .Overlay_out0(NewRow0), .Overlay_out1(NewRow1), .Overlay_out2(NewRow2),
    .Overlay_out3(NewRow3), .Overlay_out4(NewRow4), .Overlay_out5(NewRow5), .Overlay_out6(NewRow6),
    .Overlay_out7(NewRow7), .Overlay_out8(NewRow8), .Overlay_out9(NewRow9), .Overlay_out10(NewRow10),
    .Overlay_out11(NewRow11), .Overlay_out12(NewRow12), .Overlay_out13(NewRow13), .Overlay_out14(NewRow14),
    .Overlay_out15(NewRow15), .Overlay_out16(NewRow16), .Overlay_out17(NewRow17), .Overlay_out18(NewRow18),
    .Overlay_out19(NewRow19), .OutputRow0(Row0), .OutputRow1(Row1), .OutputRow2(Row2), .OutputRow3(Row3),
    .OutputRow4(Row4), .OutputRow5(Row5), .OutputRow6(Row6), .OutputRow7(Row7), .OutputRow8(Row8),
    .OutputRow9(Row9), .OutputRow10(Row10), .OutputRow11(Row11), .OutputRow12(Row12), .OutputRow13(Row13),
    .OutputRow14(Row14), .OutputRow15(Row15), .OutputRow16(Row16), .OutputRow17(Row17), .OutputRow18(Row18),
    .OutputRow19(Row19));
  Tetromino_Rom tetromino_rom_1 (
    .Rotate(Rotate), .Rotate_OK(Rotate_OK), .BlockType(Random_Block), .Shape_out(Shape_out),
    .XYlength(XY_length), .Next_Rotate(Next_Rotate), .Next_Length(Next_Length));
  LineClear lineclear_1 (
    .Overlay_out0(Overlay_Out0), .Overlay_out1(Overlay_Out1), .Overlay_out2(Overlay_Out2),
    .Overlay_out3(Overlay_Out3), .Overlay_out4(Overlay_Out4), .Overlay_out5(Overlay_Out5),
    .Overlay_out6(Overlay_Out6), .Overlay_out7(Overlay_Out7), .Overlay_out8(Overlay_Out8),
    .Overlay_out9(Overlay_Out9), .Overlay_out10(Overlay_Out10), .Overlay_out11(Overlay_Out11),
    .Overlay_out12(Overlay_Out12), .Overlay_out13(Overlay_Out13), .Overlay_out14(Overlay_Out14),
    .Overlay_out15(Overlay_Out15), .Overlay_out16(Overlay_Out16), .Overlay_out17(Overlay_Out17),
    .Overlay_out18(Overlay_Out18), .Overlay_out19(Overlay_Out19), .NewRow0(NewRow0), .NewRow1(NewRow1),
    .NewRow2(NewRow2), .NewRow3(NewRow3), .NewRow4(NewRow4), .NewRow5(NewRow5), .NewRow6(NewRow6),
    .NewRow7(NewRow7), .NewRow8(NewRow8), .NewRow9(NewRow9), .NewRow10(NewRow10), .NewRow11(NewRow11),
    .NewRow12(NewRow12), .NewRow13(NewRow13), .NewRow14(NewRow14), .NewRow15(NewRow15), .NewRow16(NewRow16),
    .NewRow17(NewRow17), .NewRow18(NewRow18), .NewRow19(NewRow19), .AddScore(AddScore));
  Clock clock_1 (.out(clock_1_out));
  Block_Overlay_All block_overlay_all_1 (
    .Shape_out(Shape_out), .Block_X(Block_X), .Block_Y(Block_Y), .Row0(Row0), .Row1(Row1), .Row2(Row2),
    .Row3(Row3), .Row4(Row4), .Row5(Row5), .Row6(Row6), .Row7(Row7), .Row8(Row8), .Row9(Row9), .Row10(Row10),
    .Row11(Row11), .Row12(Row12), .Row13(Row13), .Row14(Row14), .Row15(Row15), .Row16(Row16), .Row17(Row17),
    .Row18(Row18), .Row19(Row19), .Out0(Overlay_Out0), .Out1(Overlay_Out1), .Out2(Overlay_Out2),
    .Out3(Overlay_Out3), .Out4(Overlay_Out4), .Out5(Overlay_Out5), .Out6(Overlay_Out6), .Out7(Overlay_Out7),
    .Out8(Overlay_Out8), .Out9(Overlay_Out9), .Out10(Overlay_Out10), .Out11(Overlay_Out11),
    .Out12(Overlay_Out12), .Out13(Overlay_Out13), .Out14(Overlay_Out14), .Out15(Overlay_Out15),
    .Out16(Overlay_Out16), .Out17(Overlay_Out17), .Out18(Overlay_Out18), .Out19(Overlay_Out19));
  Clockdevide clockdevide_1 (.Clock(clock_1_out), .LV(LV), .FastClock(FastClock), .SlowClock(SlowClock));
endmodule

module Xdecoder (
  input  Enable,
  input  [3:0] in_2,
  output [9:0] out_3
);

  Decoder #(.select(4)) decoder_1 (
    .out0(out_3[0]), .out1(out_3[1]), .out2(out_3[2]), .out3(out_3[3]), .out4(out_3[4]), .out5(out_3[5]),
    .out6(out_3[6]), .out7(out_3[7]), .out8(out_3[8]), .out9(out_3[9]), .sel(in_2), .en(Enable));  // open: out10, out11, out12, out13, out14, out15
endmodule

module Ydecoder (
  input  Enable,
  input  [4:0] in_2,
  output [19:0] out_3
);

  Decoder #(.select(5)) decoder_1 (
    .out0(out_3[0]), .out1(out_3[1]), .out2(out_3[2]), .out3(out_3[3]), .out4(out_3[4]), .out5(out_3[5]),
    .out6(out_3[6]), .out7(out_3[7]), .out8(out_3[8]), .out9(out_3[9]), .out10(out_3[10]), .out11(out_3[11]),
    .out12(out_3[12]), .out13(out_3[13]), .out14(out_3[14]), .out15(out_3[15]), .out16(out_3[16]),
    .out17(out_3[17]), .out18(out_3[18]), .out19(out_3[19]), .sel(in_2), .en(Enable));  // open: out20, out21, out22, out23, out24, out25, out26, out27, out28, out29, out30, out31
endmodule

module Block_Control (
  input  Left,
  input  Left_OK,
  input  Right,
  input  Right_OK,
  input  Down,
  input  Down_OK,
  input  FastClock,
  input  SlowClock,
  output [3:0] X_out,
  output [4:0] Y_out,
  output Reset,
  output GMClock,
  output Lock,
  output GameOver
);

  wire and_3_out, and_6_out, and_7_out, and_8_out, and_9_out, and_10_out, comparator_1_lt, comparator_2_lt,
       d_ff_1_q, d_ff_2_q, d_ff_3_q, d_ff_5_q, d_ff_7_q, Init, left_t, LeftPulse, not_1_out, not_2_out,
       not_3_out, not_4_out, not_5_out, not_6_out, not_8_out, or_2_out, right_t, RightPulse;
  wire [3:0] adder_1_out, multiplexer_1_out, multiplexer_2_out;
  wire [4:0] adder_2_out;

  not not_1 (not_1_out, Lock);
  and and_1 (left_t, Left, Left_OK);
  and and_2 (right_t, Right, Right_OK);
  D_Flip_Flop d_ff_1 (.D(left_t), .clk(FastClock), .Q(d_ff_1_q));  // open: Qn, preset, reset
  D_Flip_Flop d_ff_2 (.D(right_t), .clk(FastClock), .Q(d_ff_2_q));  // open: Qn, preset, reset
  and and_3 (and_3_out, Down, not_1_out);
  D_Flip_Flop d_ff_3 (.D(and_3_out), .clk(FastClock), .Q(d_ff_3_q));  // open: Qn, preset, reset
  and and_4 (LeftPulse, left_t, not_2_out);
  not not_2 (not_2_out, d_ff_1_q);
  and and_5 (RightPulse, right_t, not_3_out);
  not not_3 (not_3_out, d_ff_2_q);
  not not_4 (not_4_out, d_ff_3_q);
  D_Flip_Flop d_ff_4 ();  // open: D, clk, Q, Qn, preset, reset
  D_Flip_Flop d_ff_5 (.D(and_6_out), .clk(FastClock), .Q(d_ff_5_q));  // open: Qn, preset, reset
  and and_6 (and_6_out, and_3_out, not_4_out);
  Multiplexer #(.select(2), .width(4)) multiplexer_1 (
    .in0(4'b0000), .in1(4'b0001), .in2(4'b1111), .in3(4'b0000), .out(multiplexer_1_out),
    .sel({RightPulse, LeftPulse}));
  not not_5 (not_5_out, d_ff_5_q);
  Adder #(.width(4)) adder_1 (.a(X_out), .b(multiplexer_1_out), .out(adder_1_out));  // open: cin, cout
  or or_1 (GMClock, and_6_out, and_7_out);
  and and_7 (and_7_out, not_5_out, SlowClock);
  Comparator #(.mode("unsigned"), .width(4)) comparator_1 (
    .a(adder_1_out), .b(4'b1010), .lt(comparator_1_lt));  // open: gt, eq
  not not_6 (not_6_out, Lock);
  Register #(.width(4)) Xregister (.D(multiplexer_2_out), .en(and_8_out), .clk(FastClock), .Q(X_out));  // open: clr
  Multiplexer #(.width(4)) multiplexer_2 (.in0(adder_1_out), .in1(4'b0011), .out(multiplexer_2_out), .sel(or_2_out));
  and and_8 (and_8_out, comparator_1_lt, not_6_out);
  Adder #(.width(5)) adder_2 (.a(Y_out), .b(5'b00001), .out(adder_2_out));  // open: cin, cout
  or or_2 (or_2_out, Init, Reset);
  Register #(.width(5)) Yregister (.D(adder_2_out), .en(and_9_out), .clk(GMClock), .Q(Y_out), .clr(Reset));
  Comparator #(.mode("unsigned"), .width(5)) comparator_2 (
    .a(adder_2_out), .b(5'b10100), .lt(comparator_2_lt));  // open: gt, eq
  and and_9 (and_9_out, comparator_2_lt, Down_OK);
  D_Flip_Flop d_ff_6 (.D(Lock), .clk(SlowClock), .Q(Reset));  // open: Qn, preset, reset
  D_Flip_Flop d_ff_7 (.D(1'b1), .clk(FastClock), .Q(d_ff_7_q));  // open: Qn, preset, reset
  not not_7 (Init, d_ff_7_q);
  Down_Lock down_lock_1 (.Down_OK(Down_OK), .ClockD16(GMClock), .Lock(Lock));
  D_Flip_Flop d_ff_8 (.D(and_10_out), .clk(SlowClock), .Q(GameOver));  // open: Qn, preset, reset
  and and_10 (and_10_out, Reset, not_8_out);
  not not_8 (not_8_out, Down_OK);

  // Other names for the same wires on the sheet: Clock = GMClock
endmodule

module GameMemory (
  input  Clock,
  input  Lock,
  input  [9:0] Overlay_out0,
  input  [9:0] Overlay_out1,
  input  [9:0] Overlay_out2,
  input  [9:0] Overlay_out3,
  input  [9:0] Overlay_out4,
  input  [9:0] Overlay_out5,
  input  [9:0] Overlay_out6,
  input  [9:0] Overlay_out7,
  input  [9:0] Overlay_out8,
  input  [9:0] Overlay_out9,
  input  [9:0] Overlay_out10,
  input  [9:0] Overlay_out11,
  input  [9:0] Overlay_out12,
  input  [9:0] Overlay_out13,
  input  [9:0] Overlay_out14,
  input  [9:0] Overlay_out15,
  input  [9:0] Overlay_out16,
  input  [9:0] Overlay_out17,
  input  [9:0] Overlay_out18,
  input  [9:0] Overlay_out19,
  output [9:0] OutputRow0,
  output [9:0] OutputRow1,
  output [9:0] OutputRow2,
  output [9:0] OutputRow3,
  output [9:0] OutputRow4,
  output [9:0] OutputRow5,
  output [9:0] OutputRow6,
  output [9:0] OutputRow7,
  output [9:0] OutputRow8,
  output [9:0] OutputRow9,
  output [9:0] OutputRow10,
  output [9:0] OutputRow11,
  output [9:0] OutputRow12,
  output [9:0] OutputRow13,
  output [9:0] OutputRow14,
  output [9:0] OutputRow15,
  output [9:0] OutputRow16,
  output [9:0] OutputRow17,
  output [9:0] OutputRow18,
  output [9:0] OutputRow19
);

  Register #(.width(10)) Row0 (.D(Overlay_out0), .en(Lock), .clk(Clock), .Q(OutputRow0));  // open: clr
  Register #(.width(10)) Row10 (.D(Overlay_out10), .en(Lock), .clk(Clock), .Q(OutputRow10));  // open: clr
  Register #(.width(10)) Row1 (.D(Overlay_out1), .en(Lock), .clk(Clock), .Q(OutputRow1));  // open: clr
  Register #(.width(10)) Row11 (.D(Overlay_out11), .en(Lock), .clk(Clock), .Q(OutputRow11));  // open: clr
  Register #(.width(10)) Row2 (.D(Overlay_out2), .en(Lock), .clk(Clock), .Q(OutputRow2));  // open: clr
  Register #(.width(10)) Row12 (.D(Overlay_out12), .en(Lock), .clk(Clock), .Q(OutputRow12));  // open: clr
  Register #(.width(10)) Row3 (.D(Overlay_out3), .en(Lock), .clk(Clock), .Q(OutputRow3));  // open: clr
  Register #(.width(10)) Row13 (.D(Overlay_out13), .en(Lock), .clk(Clock), .Q(OutputRow13));  // open: clr
  Register #(.width(10)) Row4 (.D(Overlay_out4), .en(Lock), .clk(Clock), .Q(OutputRow4));  // open: clr
  Register #(.width(10)) Row14 (.D(Overlay_out14), .en(Lock), .clk(Clock), .Q(OutputRow14));  // open: clr
  Register #(.width(10)) Row5 (.D(Overlay_out5), .en(Lock), .clk(Clock), .Q(OutputRow5));  // open: clr
  Register #(.width(10)) Row15 (.D(Overlay_out15), .en(Lock), .clk(Clock), .Q(OutputRow15));  // open: clr
  Register #(.width(10)) Row6 (.D(Overlay_out6), .en(Lock), .clk(Clock), .Q(OutputRow6));  // open: clr
  Register #(.width(10)) Row16 (.D(Overlay_out16), .en(Lock), .clk(Clock), .Q(OutputRow16));  // open: clr
  Register #(.width(10)) Row7 (.D(Overlay_out7), .en(Lock), .clk(Clock), .Q(OutputRow7));  // open: clr
  Register #(.width(10)) Row17 (.D(Overlay_out17), .en(Lock), .clk(Clock), .Q(OutputRow17));  // open: clr
  Register #(.width(10)) Row8 (.D(Overlay_out8), .en(Lock), .clk(Clock), .Q(OutputRow8));  // open: clr
  Register #(.width(10)) Row18 (.D(Overlay_out18), .en(Lock), .clk(Clock), .Q(OutputRow18));  // open: clr
  Register #(.width(10)) Row9 (.D(Overlay_out9), .en(Lock), .clk(Clock), .Q(OutputRow9));  // open: clr
  Register #(.width(10)) Row19 (.D(Overlay_out19), .en(Lock), .clk(Clock), .Q(OutputRow19));  // open: clr

  // Other names for the same wires on the sheet: Row0[9:0] = Overlay_out0; Row1[9:0] = Overlay_out1;
  //   Row2[9:0] = Overlay_out2; Row3[9:0] = Overlay_out3; Row4[9:0] = Overlay_out4; Row5[9:0] = Overlay_out5;
  //   Row6[9:0] = Overlay_out6; Row7[9:0] = Overlay_out7; Row8[9:0] = Overlay_out8; Row9[9:0] = Overlay_out9;
  //   Row10[9:0] = Overlay_out10; Row11[9:0] = Overlay_out11; Row12[9:0] = Overlay_out12; Row13[9:0] = Overlay_out13;
  //   Row14[9:0] = Overlay_out14; Row15[9:0] = Overlay_out15; Row16[9:0] = Overlay_out16; Row17[9:0] = Overlay_out17;
  //   Row18[9:0] = Overlay_out18; Row19[9:0] = Overlay_out19
endmodule

module Tetromino_Rom (
  input  Rotate,
  input  Rotate_OK,
  input  [2:0] BlockType,
  output [15:0] Shape_out,
  output [3:0] XYlength,
  output [15:0] Next_Rotate,
  output [3:0] Next_Length
);

  wire comparator_1_eq, Rotate_t;
  wire [1:0] adder_1_out, adder_2_out, multiplexer_1_out, Turn_num;

  Register #(.width(2)) register_1 (.D(multiplexer_1_out), .clk(Rotate_t), .Q(Turn_num));  // open: en, clr
  and and_1 (Rotate_t, Rotate, Rotate_OK);
  Adder #(.width(2)) adder_1 (.a(Turn_num), .b(2'b01), .out(adder_1_out));  // open: cin, cout
  Adder #(.width(2)) adder_2 (.a(Turn_num), .b(2'b01), .out(adder_2_out));  // open: cin, cout
  Multiplexer #(.width(2)) multiplexer_1 (
    .in0(adder_1_out), .in1(2'b00), .out(multiplexer_1_out), .sel(comparator_1_eq));
  Comparator #(.width(2)) comparator_1 (.a(Turn_num), .b(2'b11), .eq(comparator_1_eq));  // open: gt, lt
  ROM #(.addrWidth(5), .dataWidth(16)) rom_1 (.addr({BlockType, Turn_num}), .data(Shape_out));
  ROM #(.addrWidth(5), .dataWidth(4)) rom_2 (.addr({BlockType, Turn_num}), .data(XYlength));
  ROM #(.addrWidth(5), .dataWidth(16)) rom_3 (.addr({BlockType, adder_2_out}), .data(Next_Rotate));
  ROM #(.addrWidth(5), .dataWidth(4)) rom_4 (.addr({BlockType, adder_2_out}), .data(Next_Length));

  // Notes on the sheet:
  //   contents of rom_1 (hex, n*v repeats v):
  //   f000 1111 f000 1111 4*3300 7200 1310 2700 2320 2230 1700 3110 7400 1130 7100 3220 4700 6300 1320
  //   6300 1320 3600 2310 3600 2310
  //   contents of rom_2 (hex, n*v repeats v):
  //   c 3 c 3 4*5 9 6 9 6 6 9 6 9 6 9 6 9 9 6 9 6 9 6 9 6
  //   contents of rom_3 (hex, n*v repeats v):
  //   f000 1111 f000 1111 4*3300 7200 1310 2700 2320 2230 1700 3110 7400 1130 7100 3220 4700 6300 1320
  //   6300 1320 3600 2310 3600 2310
  //   contents of rom_4 (hex, n*v repeats v):
  //   c 3 c 3 4*5 9 6 9 6 6 9 6 9 6 9 6 9 9 6 9 6 9 6 9 6
endmodule

module Block_Overlay (
  input  [15:0] Shape_out,
  input  [3:0] Block_X,
  input  [4:0] Block_Y,
  input  [4:0] Row_Num,
  input  [9:0] Row_Data,
  output [9:0] Overlay_out
);

  wire comparator_1_eq, comparator_2_eq, comparator_3_eq, comparator_4_eq;
  wire [4:0] Y1, Y2, Y3;
  wire [9:0] bit_extender_1_out, bit_extender_2_out, bit_extender_3_out, bit_extender_4_out,
       multiplexer_1_out, multiplexer_2_out, multiplexer_3_out, multiplexer_4_out, or_1_out, shifter_1_out,
       shifter_2_out, shifter_3_out, shifter_4_out;

  Adder #(.width(5)) adder_1 (.a(Block_Y), .b(5'b00001), .out(Y1));  // open: cin, cout
  Adder #(.width(5)) adder_2 (.a(Block_Y), .b(5'b00010), .out(Y2));  // open: cin, cout
  Adder #(.width(5)) adder_3 (.a(Block_Y), .b(5'b00011), .out(Y3));  // open: cin, cout
  assign bit_extender_1_out = {{6{1'b0}}, Shape_out[3:0]};  // Bit_Extender bit_extender_1
  assign bit_extender_2_out = {{6{1'b0}}, Shape_out[7:4]};  // Bit_Extender bit_extender_2
  assign bit_extender_3_out = {{6{1'b0}}, Shape_out[11:8]};  // Bit_Extender bit_extender_3
  assign bit_extender_4_out = {{6{1'b0}}, Shape_out[15:12]};  // Bit_Extender bit_extender_4
  Comparator #(.width(5)) comparator_1 (.a(Row_Num), .b(Block_Y), .eq(comparator_1_eq));  // open: gt, lt
  Comparator #(.width(5)) comparator_2 (.a(Row_Num), .b(Y1), .eq(comparator_2_eq));  // open: gt, lt
  Comparator #(.width(5)) comparator_3 (.a(Row_Num), .b(Y2), .eq(comparator_3_eq));  // open: gt, lt
  Comparator #(.width(5)) comparator_4 (.a(Row_Num), .b(Y3), .eq(comparator_4_eq));  // open: gt, lt
  Shifter #(.width(10)) shifter_1 (.in(bit_extender_1_out), .\dist (Block_X), .out(shifter_1_out));
  Shifter #(.width(10)) shifter_2 (.in(bit_extender_2_out), .\dist (Block_X), .out(shifter_2_out));
  Shifter #(.width(10)) shifter_3 (.in(bit_extender_3_out), .\dist (Block_X), .out(shifter_3_out));
  Shifter #(.width(10)) shifter_4 (.in(bit_extender_4_out), .\dist (Block_X), .out(shifter_4_out));
  Multiplexer #(.width(10)) multiplexer_1 (
    .in0({10{1'b0}}), .in1(shifter_4_out), .out(multiplexer_1_out), .sel(comparator_1_eq));
  Multiplexer #(.width(10)) multiplexer_2 (
    .in0({10{1'b0}}), .in1(shifter_3_out), .out(multiplexer_2_out), .sel(comparator_2_eq));
  Multiplexer #(.width(10)) multiplexer_3 (
    .in0({10{1'b0}}), .in1(shifter_2_out), .out(multiplexer_3_out), .sel(comparator_3_eq));
  Multiplexer #(.width(10)) multiplexer_4 (
    .in0({10{1'b0}}), .in1(shifter_1_out), .out(multiplexer_4_out), .sel(comparator_4_eq));
  assign or_1_out = multiplexer_1_out | multiplexer_2_out | multiplexer_3_out | multiplexer_4_out;  // OR_Gate or_1, 10 bits wide
  assign Overlay_out = or_1_out | Row_Data;  // OR_Gate or_2, 10 bits wide

  // Other names for the same wires on the sheet: Shape_Row3[3:0] = Shape_out[3:0]; Shape_Row2[3:0] = Shape_out[7:4];
  //   Shape_Row1[3:0] = Shape_out[11:8]; Shape_Row0[3:0] = Shape_out[15:12]; Y0[4:0] = Block_Y
endmodule

module Block_Overlay_All (
  input  [15:0] Shape_out,
  input  [3:0] Block_X,
  input  [4:0] Block_Y,
  input  [9:0] Row0,
  input  [9:0] Row1,
  input  [9:0] Row2,
  input  [9:0] Row3,
  input  [9:0] Row4,
  input  [9:0] Row5,
  input  [9:0] Row6,
  input  [9:0] Row7,
  input  [9:0] Row8,
  input  [9:0] Row9,
  input  [9:0] Row10,
  input  [9:0] Row11,
  input  [9:0] Row12,
  input  [9:0] Row13,
  input  [9:0] Row14,
  input  [9:0] Row15,
  input  [9:0] Row16,
  input  [9:0] Row17,
  input  [9:0] Row18,
  input  [9:0] Row19,
  output [9:0] Out0,
  output [9:0] Out1,
  output [9:0] Out2,
  output [9:0] Out3,
  output [9:0] Out4,
  output [9:0] Out5,
  output [9:0] Out6,
  output [9:0] Out7,
  output [9:0] Out8,
  output [9:0] Out9,
  output [9:0] Out10,
  output [9:0] Out11,
  output [9:0] Out12,
  output [9:0] Out13,
  output [9:0] Out14,
  output [9:0] Out15,
  output [9:0] Out16,
  output [9:0] Out17,
  output [9:0] Out18,
  output [9:0] Out19
);

  Block_Overlay block_overlay_1 (
    .Shape_out(Shape_out), .Block_X(Block_X), .Block_Y(Block_Y), .Row_Num({5{1'b0}}), .Row_Data(Row0),
    .Overlay_out(Out0));
  Block_Overlay block_overlay_2 (
    .Shape_out(Shape_out), .Block_X(Block_X), .Block_Y(Block_Y), .Row_Num(5'b00001), .Row_Data(Row1),
    .Overlay_out(Out1));
  Block_Overlay block_overlay_3 (
    .Shape_out(Shape_out), .Block_X(Block_X), .Block_Y(Block_Y), .Row_Num(5'b00010), .Row_Data(Row2),
    .Overlay_out(Out2));
  Block_Overlay block_overlay_4 (
    .Shape_out(Shape_out), .Block_X(Block_X), .Block_Y(Block_Y), .Row_Num(5'b00011), .Row_Data(Row3),
    .Overlay_out(Out3));
  Block_Overlay block_overlay_5 (
    .Shape_out(Shape_out), .Block_X(Block_X), .Block_Y(Block_Y), .Row_Num(5'b00100), .Row_Data(Row4),
    .Overlay_out(Out4));
  Block_Overlay block_overlay_6 (
    .Shape_out(Shape_out), .Block_X(Block_X), .Block_Y(Block_Y), .Row_Num(5'b00101), .Row_Data(Row5),
    .Overlay_out(Out5));
  Block_Overlay block_overlay_7 (
    .Shape_out(Shape_out), .Block_X(Block_X), .Block_Y(Block_Y), .Row_Num(5'b00110), .Row_Data(Row6),
    .Overlay_out(Out6));
  Block_Overlay block_overlay_8 (
    .Shape_out(Shape_out), .Block_X(Block_X), .Block_Y(Block_Y), .Row_Num(5'b00111), .Row_Data(Row7),
    .Overlay_out(Out7));
  Block_Overlay block_overlay_9 (
    .Shape_out(Shape_out), .Block_X(Block_X), .Block_Y(Block_Y), .Row_Num(5'b01000), .Row_Data(Row8),
    .Overlay_out(Out8));
  Block_Overlay block_overlay_10 (
    .Shape_out(Shape_out), .Block_X(Block_X), .Block_Y(Block_Y), .Row_Num(5'b01001), .Row_Data(Row9),
    .Overlay_out(Out9));
  Block_Overlay block_overlay_11 (
    .Shape_out(Shape_out), .Block_X(Block_X), .Block_Y(Block_Y), .Row_Num(5'b01010), .Row_Data(Row10),
    .Overlay_out(Out10));
  Block_Overlay block_overlay_12 (
    .Shape_out(Shape_out), .Block_X(Block_X), .Block_Y(Block_Y), .Row_Num(5'b01011), .Row_Data(Row11),
    .Overlay_out(Out11));
  Block_Overlay block_overlay_13 (
    .Shape_out(Shape_out), .Block_X(Block_X), .Block_Y(Block_Y), .Row_Num(5'b01100), .Row_Data(Row12),
    .Overlay_out(Out12));
  Block_Overlay block_overlay_14 (
    .Shape_out(Shape_out), .Block_X(Block_X), .Block_Y(Block_Y), .Row_Num(5'b01101), .Row_Data(Row13),
    .Overlay_out(Out13));
  Block_Overlay block_overlay_15 (
    .Shape_out(Shape_out), .Block_X(Block_X), .Block_Y(Block_Y), .Row_Num(5'b01110), .Row_Data(Row14),
    .Overlay_out(Out14));
  Block_Overlay block_overlay_16 (
    .Shape_out(Shape_out), .Block_X(Block_X), .Block_Y(Block_Y), .Row_Num(5'b01111), .Row_Data(Row15),
    .Overlay_out(Out15));
  Block_Overlay block_overlay_17 (
    .Shape_out(Shape_out), .Block_X(Block_X), .Block_Y(Block_Y), .Row_Num(5'b10000), .Row_Data(Row16),
    .Overlay_out(Out16));
  Block_Overlay block_overlay_18 (
    .Shape_out(Shape_out), .Block_X(Block_X), .Block_Y(Block_Y), .Row_Num(5'b10001), .Row_Data(Row17),
    .Overlay_out(Out17));
  Block_Overlay block_overlay_19 (
    .Shape_out(Shape_out), .Block_X(Block_X), .Block_Y(Block_Y), .Row_Num(5'b10010), .Row_Data(Row18),
    .Overlay_out(Out18));
  Block_Overlay block_overlay_20 (
    .Shape_out(Shape_out), .Block_X(Block_X), .Block_Y(Block_Y), .Row_Num(5'b10011), .Row_Data(Row19),
    .Overlay_out(Out19));
endmodule

// Row
module Collision_Detector (
  input  [15:0] Shape_out,
  input  [15:0] Next_Rotate,
  input  [3:0] Block_X,
  input  [4:0] Block_Y,
  input  [3:0] XYlength,
  input  [3:0] Next_Length,
  input  [9:0] Row0,
  input  [9:0] Row1,
  input  [9:0] Row2,
  input  [9:0] Row3,
  input  [9:0] Row4,
  input  [9:0] Row5,
  input  [9:0] Row6,
  input  [9:0] Row7,
  input  [9:0] Row8,
  input  [9:0] Row9,
  input  [9:0] Row10,
  input  [9:0] Row11,
  input  [9:0] Row12,
  input  [9:0] Row13,
  input  [9:0] Row14,
  input  [9:0] Row15,
  input  [9:0] Row16,
  input  [9:0] Row17,
  input  [9:0] Row18,
  input  [9:0] Row19,
  output Right_OK,
  output Left_OK,
  output Down_OK,
  output Rotate_OK
);

  wire comparator_1_eq, comparator_2_lt, comparator_3_lt, comparator_4_lt, comparator_5_lt, not_1_out,
       not_2_out, not_3_out, or_5_out, or_6_out, or_7_out, or_8_out, or_9_out;
  wire [3:0] adder_5_out, adder_6_out, adder_7_out, adder_9_out, bit_extender_17_out, bit_extender_19_out;
  wire [4:0] adder_8_out, adder_10_out, bit_extender_18_out, bit_extender_20_out, Y1, Y2, Y3, Y4;
  wire [9:0] and_1_out, and_2_out, and_3_out, and_4_out, and_5_out, and_6_out, and_7_out, and_8_out,
       and_9_out, and_10_out, and_11_out, and_12_out, and_13_out, and_14_out, and_15_out, and_16_out,
       bit_extender_1_out, bit_extender_2_out, bit_extender_3_out, bit_extender_4_out, bit_extender_5_out,
       bit_extender_6_out, bit_extender_7_out, bit_extender_8_out, bit_extender_9_out, bit_extender_10_out,
       bit_extender_11_out, bit_extender_12_out, bit_extender_13_out, bit_extender_14_out,
       bit_extender_15_out, bit_extender_16_out, MUX_Y0, MUX_Y1, MUX_Y2, MUX_Y3, MUX_Y4, or_1_out, or_2_out,
       or_3_out, or_4_out, shifter_1_out, shifter_2_out, shifter_3_out, shifter_4_out, shifter_5_out,
       shifter_6_out, shifter_7_out, shifter_8_out, shifter_9_out, shifter_10_out, shifter_11_out,
       shifter_12_out, shifter_13_out, shifter_14_out, shifter_15_out, shifter_16_out;

  Adder #(.width(5)) adder_1 (.a(Block_Y), .b(5'b00001), .out(Y1));  // open: cin, cout
  Adder #(.width(5)) adder_2 (.a(Block_Y), .b(5'b00010), .out(Y2));  // open: cin, cout
  Adder #(.width(5)) adder_3 (.a(Block_Y), .b(5'b00011), .out(Y3));  // open: cin, cout
  Adder #(.width(5)) adder_4 (.a(Block_Y), .b(5'b00100), .out(Y4));  // open: cin, cout
  Multiplexer #(.select(5), .width(10)) multiplexer_1 (
    .in0(Row0), .in1(Row1), .in2(Row2), .in3(Row3), .in4(Row4), .in5(Row5), .in6(Row6), .in7(Row7),
    .in8(Row8), .in9(Row9), .in10(Row10), .in11(Row11), .in12(Row12), .in13(Row13), .in14(Row14),
    .in15(Row15), .in16(Row16), .in17(Row17), .in18(Row18), .in19(Row19), .out(MUX_Y0), .sel(Block_Y));  // open: in20, in21, in22, in23, in24, in25, in26, in27, in28, in29, in30, in31
  Adder #(.width(4)) adder_5 (.a(Block_X), .b(4'b1111), .out(adder_5_out));  // open: cin, cout
  assign bit_extender_1_out = {{6{1'b0}}, Shape_out[3:0]};  // Bit_Extender bit_extender_1
  assign bit_extender_2_out = {{6{1'b0}}, Shape_out[7:4]};  // Bit_Extender bit_extender_2
  assign bit_extender_3_out = {{6{1'b0}}, Shape_out[11:8]};  // Bit_Extender bit_extender_3
  assign bit_extender_4_out = {{6{1'b0}}, Shape_out[15:12]};  // Bit_Extender bit_extender_4
  Adder #(.width(4)) adder_6 (.a(Block_X), .b(4'b0001), .out(adder_6_out));  // open: cin, cout
  assign bit_extender_5_out = {{6{1'b0}}, Shape_out[3:0]};  // Bit_Extender bit_extender_5
  assign bit_extender_6_out = {{6{1'b0}}, Shape_out[7:4]};  // Bit_Extender bit_extender_6
  assign bit_extender_7_out = {{6{1'b0}}, Shape_out[11:8]};  // Bit_Extender bit_extender_7
  assign bit_extender_8_out = {{6{1'b0}}, Shape_out[15:12]};  // Bit_Extender bit_extender_8
  assign bit_extender_9_out = {{6{1'b0}}, Shape_out[3:0]};  // Bit_Extender bit_extender_9
  assign bit_extender_10_out = {{6{1'b0}}, Shape_out[7:4]};  // Bit_Extender bit_extender_10
  assign bit_extender_11_out = {{6{1'b0}}, Shape_out[11:8]};  // Bit_Extender bit_extender_11
  assign bit_extender_12_out = {{6{1'b0}}, Shape_out[15:12]};  // Bit_Extender bit_extender_12
  assign bit_extender_13_out = {{6{1'b0}}, Next_Rotate[3:0]};  // Bit_Extender bit_extender_13
  assign bit_extender_14_out = {{6{1'b0}}, Next_Rotate[7:4]};  // Bit_Extender bit_extender_14
  assign bit_extender_15_out = {{6{1'b0}}, Next_Rotate[11:8]};  // Bit_Extender bit_extender_15
  assign bit_extender_16_out = {{6{1'b0}}, Next_Rotate[15:12]};  // Bit_Extender bit_extender_16
  Multiplexer #(.select(5), .width(10)) multiplexer_2 (
    .in0(Row0), .in1(Row1), .in2(Row2), .in3(Row3), .in4(Row4), .in5(Row5), .in6(Row6), .in7(Row7),
    .in8(Row8), .in9(Row9), .in10(Row10), .in11(Row11), .in12(Row12), .in13(Row13), .in14(Row14),
    .in15(Row15), .in16(Row16), .in17(Row17), .in18(Row18), .in19(Row19), .out(MUX_Y1), .sel(Y1));  // open: in20, in21, in22, in23, in24, in25, in26, in27, in28, in29, in30, in31
  Shifter #(.width(10)) shifter_1 (.in(bit_extender_1_out), .\dist (adder_5_out), .out(shifter_1_out));
  Shifter #(.width(10)) shifter_2 (.in(bit_extender_2_out), .\dist (adder_5_out), .out(shifter_2_out));
  Shifter #(.width(10)) shifter_3 (.in(bit_extender_3_out), .\dist (adder_5_out), .out(shifter_3_out));
  Shifter #(.width(10)) shifter_4 (.in(bit_extender_4_out), .\dist (adder_5_out), .out(shifter_4_out));
  Shifter #(.width(10)) shifter_5 (.in(bit_extender_5_out), .\dist (adder_6_out), .out(shifter_5_out));
  Shifter #(.width(10)) shifter_6 (.in(bit_extender_6_out), .\dist (adder_6_out), .out(shifter_6_out));
  Shifter #(.width(10)) shifter_7 (.in(bit_extender_7_out), .\dist (adder_6_out), .out(shifter_7_out));
  Shifter #(.width(10)) shifter_8 (.in(bit_extender_8_out), .\dist (adder_6_out), .out(shifter_8_out));
  Shifter #(.width(10)) shifter_9 (.in(bit_extender_9_out), .\dist (Block_X), .out(shifter_9_out));
  Shifter #(.width(10)) shifter_10 (.in(bit_extender_10_out), .\dist (Block_X), .out(shifter_10_out));
  Shifter #(.width(10)) shifter_11 (.in(bit_extender_11_out), .\dist (Block_X), .out(shifter_11_out));
  Shifter #(.width(10)) shifter_12 (.in(bit_extender_12_out), .\dist (Block_X), .out(shifter_12_out));
  Shifter #(.width(10)) shifter_13 (.in(bit_extender_13_out), .\dist (Block_X), .out(shifter_13_out));
  Shifter #(.width(10)) shifter_14 (.in(bit_extender_14_out), .\dist (Block_X), .out(shifter_14_out));
  Shifter #(.width(10)) shifter_15 (.in(bit_extender_15_out), .\dist (Block_X), .out(shifter_15_out));
  Shifter #(.width(10)) shifter_16 (.in(bit_extender_16_out), .\dist (Block_X), .out(shifter_16_out));
  assign and_1_out = shifter_1_out & MUX_Y3;  // AND_Gate and_1, 10 bits wide
  assign and_2_out = shifter_2_out & MUX_Y2;  // AND_Gate and_2, 10 bits wide
  assign and_3_out = shifter_3_out & MUX_Y1;  // AND_Gate and_3, 10 bits wide
  assign and_4_out = shifter_4_out & MUX_Y0;  // AND_Gate and_4, 10 bits wide
  assign and_5_out = shifter_5_out & MUX_Y3;  // AND_Gate and_5, 10 bits wide
  assign and_6_out = shifter_6_out & MUX_Y2;  // AND_Gate and_6, 10 bits wide
  assign and_7_out = shifter_7_out & MUX_Y1;  // AND_Gate and_7, 10 bits wide
  assign and_8_out = shifter_8_out & MUX_Y0;  // AND_Gate and_8, 10 bits wide
  Multiplexer #(.select(5), .width(10)) multiplexer_3 (
    .in0(Row0), .in1(Row1), .in2(Row2), .in3(Row3), .in4(Row4), .in5(Row5), .in6(Row6), .in7(Row7),
    .in8(Row8), .in9(Row9), .in10(Row10), .in11(Row11), .in12(Row12), .in13(Row13), .in14(Row14),
    .in15(Row15), .in16(Row16), .in17(Row17), .in18(Row18), .in19(Row19), .out(MUX_Y2), .sel(Y2));  // open: in20, in21, in22, in23, in24, in25, in26, in27, in28, in29, in30, in31
  assign or_1_out = and_1_out | and_2_out | and_3_out | and_4_out;  // OR_Gate or_1, 10 bits wide
  assign or_2_out = and_5_out | and_6_out | and_7_out | and_8_out;  // OR_Gate or_2, 10 bits wide
  assign and_9_out = shifter_9_out & MUX_Y4;  // AND_Gate and_9, 10 bits wide
  assign or_3_out = and_9_out | and_10_out | and_11_out | and_12_out;  // OR_Gate or_3, 10 bits wide
  assign and_10_out = shifter_10_out & MUX_Y3;  // AND_Gate and_10, 10 bits wide
  assign and_11_out = shifter_11_out & MUX_Y2;  // AND_Gate and_11, 10 bits wide
  assign and_12_out = shifter_12_out & MUX_Y1;  // AND_Gate and_12, 10 bits wide
  assign and_13_out = shifter_13_out & MUX_Y3;  // AND_Gate and_13, 10 bits wide
  assign and_14_out = shifter_14_out & MUX_Y2;  // AND_Gate and_14, 10 bits wide
  assign and_15_out = shifter_15_out & MUX_Y1;  // AND_Gate and_15, 10 bits wide
  assign and_16_out = shifter_16_out & MUX_Y0;  // AND_Gate and_16, 10 bits wide
  assign or_4_out = and_13_out | and_14_out | and_15_out | and_16_out;  // OR_Gate or_4, 10 bits wide
  Multiplexer #(.select(5), .width(10)) multiplexer_4 (
    .in0(Row0), .in1(Row1), .in2(Row2), .in3(Row3), .in4(Row4), .in5(Row5), .in6(Row6), .in7(Row7),
    .in8(Row8), .in9(Row9), .in10(Row10), .in11(Row11), .in12(Row12), .in13(Row13), .in14(Row14),
    .in15(Row15), .in16(Row16), .in17(Row17), .in18(Row18), .in19(Row19), .out(MUX_Y3), .sel(Y3));  // open: in20, in21, in22, in23, in24, in25, in26, in27, in28, in29, in30, in31
  or or_5 (or_5_out, or_1_out[0], or_1_out[1], or_1_out[2], or_1_out[3], or_1_out[4], or_1_out[5], or_1_out[6], or_1_out[7], or_1_out[8], or_1_out[9]);
  or or_6 (or_6_out, or_2_out[0], or_2_out[1], or_2_out[2], or_2_out[3], or_2_out[4], or_2_out[5], or_2_out[6], or_2_out[7], or_2_out[8], or_2_out[9]);
  not not_1 (not_1_out, or_6_out);
  or or_7 (or_7_out, or_3_out[0], or_3_out[1], or_3_out[2], or_3_out[3], or_3_out[4], or_3_out[5], or_3_out[6], or_3_out[7], or_3_out[8], or_3_out[9]);
  not not_2 (not_2_out, or_7_out);
  assign bit_extender_17_out = {{2{1'b0}}, Next_Length[3:2]};  // Bit_Extender bit_extender_17
  or or_8 (or_8_out, or_4_out[0], or_4_out[1], or_4_out[2], or_4_out[3], or_4_out[4], or_4_out[5], or_4_out[6], or_4_out[7], or_4_out[8], or_4_out[9]);
  assign bit_extender_18_out = {{3{1'b0}}, Next_Length[1:0]};  // Bit_Extender bit_extender_18
  Comparator #(.width(4)) comparator_1 (.a(Block_X), .b(4'b0000), .eq(comparator_1_eq));  // open: gt, lt
  assign bit_extender_19_out = {{2{1'b0}}, XYlength[3:2]};  // Bit_Extender bit_extender_19
  and and_17 (Left_OK, comparator_2_lt, not_1_out);
  assign bit_extender_20_out = {{3{1'b0}}, XYlength[1:0]};  // Bit_Extender bit_extender_20
  and and_18 (Down_OK, comparator_3_lt, not_2_out);
  Adder #(.width(4)) adder_7 (.a(Block_X), .b(bit_extender_17_out), .out(adder_7_out));  // open: cin, cout
  not not_3 (not_3_out, or_8_out);
  and and_19 (Rotate_OK, comparator_4_lt, not_3_out, comparator_5_lt);
  Adder #(.width(5)) adder_8 (.a(Block_Y), .b(bit_extender_18_out), .out(adder_8_out));  // open: cin, cout
  or or_9 (or_9_out, comparator_1_eq, or_5_out);
  not not_4 (Right_OK, or_9_out);
  Adder #(.width(4)) adder_9 (.a(Block_X), .b(bit_extender_19_out), .out(adder_9_out));  // open: cin, cout
  Comparator #(.mode("unsigned"), .width(4)) comparator_2 (
    .a(adder_9_out), .b(4'b1001), .lt(comparator_2_lt));  // open: gt, eq
  Adder #(.width(5)) adder_10 (.a(Block_Y), .b(bit_extender_20_out), .out(adder_10_out));  // open: cin, cout
  Comparator #(.mode("unsigned"), .width(5)) comparator_3 (
    .a(adder_10_out), .b(5'b10011), .lt(comparator_3_lt));  // open: gt, eq
  Comparator #(.mode("unsigned"), .width(4)) comparator_4 (
    .a(adder_7_out), .b(4'b1010), .lt(comparator_4_lt));  // open: gt, eq
  Comparator #(.mode("unsigned"), .width(5)) comparator_5 (
    .a(adder_8_out), .b(5'b10011), .lt(comparator_5_lt));  // open: gt, eq
  Multiplexer #(.select(5), .width(10)) multiplexer_5 (
    .in0(Row0), .in1(Row1), .in2(Row2), .in3(Row3), .in4(Row4), .in5(Row5), .in6(Row6), .in7(Row7),
    .in8(Row8), .in9(Row9), .in10(Row10), .in11(Row11), .in12(Row12), .in13(Row13), .in14(Row14),
    .in15(Row15), .in16(Row16), .in17(Row17), .in18(Row18), .in19(Row19), .out(MUX_Y4), .sel(Y4));  // open: in20, in21, in22, in23, in24, in25, in26, in27, in28, in29, in30, in31

  // Other names for the same wires on the sheet: NYlength[1:0] = Next_Length[1:0]; NXlength[1:0] = Next_Length[3:2];
  //   Next_Row3[3:0] = Next_Rotate[3:0]; Next_Row2[3:0] = Next_Rotate[7:4]; Next_Row1[3:0] = Next_Rotate[11:8];
  //   Next_Row0[3:0] = Next_Rotate[15:12]; Shape_Row3[3:0] = Shape_out[3:0]; Shape_Row2[3:0] = Shape_out[7:4];
  //   Shape_Row1[3:0] = Shape_out[11:8]; Shape_Row0[3:0] = Shape_out[15:12]; Ylength[1:0] = XYlength[1:0];
  //   Xlength[1:0] = XYlength[3:2]; Y0[4:0] = Block_Y
endmodule

module Clockdevide (
  input  Clock,
  input  [3:0] LV,
  output FastClock,
  output SlowClock
);

  wire d_ff_1_q, Lv0, Lv1, Lv2, Lv3, Lv4, not_1_out, not_2_out, not_3_out, not_4_out, not_5_out, not_6_out;

  not not_1 (not_1_out, d_ff_1_q);
  D_Flip_Flop d_ff_1 (.D(not_1_out), .clk(Clock), .Q(d_ff_1_q));  // open: Qn, preset, reset
  not not_2 (not_2_out, Lv4);
  D_Flip_Flop d_ff_2 (.D(not_2_out), .clk(d_ff_1_q), .Q(Lv4));  // open: Qn, preset, reset
  not not_3 (not_3_out, Lv3);
  D_Flip_Flop d_ff_3 (.D(not_3_out), .clk(Lv4), .Q(Lv3));  // open: Qn, preset, reset
  not not_4 (not_4_out, Lv2);
  D_Flip_Flop d_ff_4 (.D(not_4_out), .clk(Lv3), .Q(Lv2));  // open: Qn, preset, reset
  not not_5 (not_5_out, Lv1);
  D_Flip_Flop d_ff_5 (.D(not_5_out), .clk(Lv2), .Q(Lv1));  // open: Qn, preset, reset
  not not_6 (not_6_out, Lv0);
  D_Flip_Flop d_ff_6 (.D(not_6_out), .clk(Lv1), .Q(Lv0));  // open: Qn, preset, reset
  Multiplexer #(.select(4)) multiplexer_1 (
    .in0(Lv0), .in1(Lv1), .in2(Lv2), .in3(Lv3), .in4(Lv4), .in6(1'b0), .out(SlowClock), .sel(LV));  // open: in5, in7, in8, in9, in10, in11, in12, in13, in14, in15

  assign FastClock = Clock;
endmodule

module Down_Lock (
  input  Down_OK,
  input  ClockD16,
  output Lock
);

  wire d_ff_1_q, not_1_out, not_2_out;

  D_Flip_Flop d_ff_1 (.D(Down_OK), .clk(ClockD16), .Q(d_ff_1_q));  // open: Qn, preset, reset
  not not_1 (not_1_out, Down_OK);
  not not_2 (not_2_out, d_ff_1_q);
  and and_1 (Lock, not_1_out, not_2_out);
endmodule

module Block_Random_Generator (
  input  Lock,
  input  SlowClock,
  output [2:0] Random_Block
);

  wire Counteris7, Lock_t, Reset;
  wire [2:0] counter_1_q;
  wire [4:0] register_1_q;
  wire [7:0] random_1_out;

  D_Flip_Flop d_ff_1 (.D(Lock), .clk(SlowClock), .Q(Lock_t));  // open: Qn, preset, reset
  Random random_1 (.next(1'b1), .clk(Lock_t), .out(random_1_out));  // open: clr
  Register #(.width(5)) register_1 (.D(random_1_out[7:3]), .en(Reset), .clk(Lock_t), .Q(register_1_q));  // open: clr
  Counter #(.max('h6), .width(3)) counter_1 (
    .load(1'b0), .up(1'b1), .clk(Lock_t), .Q(counter_1_q));  // open: clr, count, D, carry
  D_Flip_Flop d_ff_2 (.D(Counteris7), .clk(Lock_t), .Q(Reset));  // open: Qn, preset, reset
  ROM #(.dataWidth(3)) rom_1 (.addr({register_1_q, counter_1_q}), .data(Random_Block));
  Comparator #(.mode("unsigned"), .width(3)) comparator_1 (
    .a(counter_1_q), .b(3'b101), .eq(Counteris7));  // open: gt, lt

  // Other names for the same wires on the sheet: Lock1 = Lock

  // Notes on the sheet:
  //   contents of rom_1 (hex, n*v repeats v):
  //   1 2 5 4 0 3 6 7 2 3 1 4 0 6 5 7 4 1 3 2 5 6 0 7 6 2 5 0 1 3 4 7 1 2 5 3 4 0 6 7 1 6 2 0 3 4 5 7 1 5
  //   3 2 0 6 4 7 4 0 1 6 3 2 5 7 6 4 2 0 3 1 5 7 6 4 5 3 1 2 0 7 6 2 4 3 5 0 1 7 2 3 6 0 5 1 4 7 6 5 0 3
  //   2 1 4 7 6 4 3 1 0 5 2 7 4 5 6 0 3 1 2 7 0 1 4 5 3 2 6 7 5 2 4 1 6 0 3 7 4 5 3 1 0 6 2 7 3 2 1 5 4 0
  //   6 7 4 0 3 1 2 5 6 7 3 4 0 2 1 6 5 7 2 5 1 4 0 3 6 7 3 4 5 1 6 2 0 7 3 0 1 4 2 5 6 7 1 5 6 3 0 2 4 7
  //   2 0 4 5 6 1 3 7 6 0 2 1 3 5 4 7 5 4 3 1 6 0 2 7 4 3 6 0 5 1 2 7 6 3 5 2 0 4 1 7 1 2 3 4 0 6 5 7 4 1
  //   6 2 5 3 0 7
endmodule

module LineClear (
  input  [9:0] Overlay_out0,
  input  [9:0] Overlay_out1,
  input  [9:0] Overlay_out2,
  input  [9:0] Overlay_out3,
  input  [9:0] Overlay_out4,
  input  [9:0] Overlay_out5,
  input  [9:0] Overlay_out6,
  input  [9:0] Overlay_out7,
  input  [9:0] Overlay_out8,
  input  [9:0] Overlay_out9,
  input  [9:0] Overlay_out10,
  input  [9:0] Overlay_out11,
  input  [9:0] Overlay_out12,
  input  [9:0] Overlay_out13,
  input  [9:0] Overlay_out14,
  input  [9:0] Overlay_out15,
  input  [9:0] Overlay_out16,
  input  [9:0] Overlay_out17,
  input  [9:0] Overlay_out18,
  input  [9:0] Overlay_out19,
  output [9:0] NewRow0,
  output [9:0] NewRow1,
  output [9:0] NewRow2,
  output [9:0] NewRow3,
  output [9:0] NewRow4,
  output [9:0] NewRow5,
  output [9:0] NewRow6,
  output [9:0] NewRow7,
  output [9:0] NewRow8,
  output [9:0] NewRow9,
  output [9:0] NewRow10,
  output [9:0] NewRow11,
  output [9:0] NewRow12,
  output [9:0] NewRow13,
  output [9:0] NewRow14,
  output [9:0] NewRow15,
  output [9:0] NewRow16,
  output [9:0] NewRow17,
  output [9:0] NewRow18,
  output [9:0] NewRow19,
  output [3:0] AddScore
);

  wire [2:0] offset0, offset1, offset2, offset3, offset4, offset5, offset6, offset7, offset8, offset9,
       offset10, offset11, offset12, offset13, offset14, offset15, offset16, offset17, offset18, offset19;
  wire [4:0] bit_extender_1_out, bit_extender_2_out, bit_extender_3_out, bit_extender_4_out,
       bit_extender_5_out, bit_extender_6_out, bit_extender_7_out, bit_extender_8_out, bit_extender_9_out,
       bit_extender_10_out, bit_extender_11_out, bit_extender_12_out, bit_extender_13_out,
       bit_extender_14_out, bit_extender_15_out, bit_extender_16_out, bit_extender_17_out,
       bit_extender_18_out, bit_extender_19_out, SrcIdx0, SrcIdx1, SrcIdx2, SrcIdx3, SrcIdx4, SrcIdx5,
       SrcIdx6, SrcIdx7, SrcIdx8, SrcIdx9, SrcIdx10, SrcIdx11, SrcIdx12, SrcIdx13, SrcIdx14, SrcIdx15,
       SrcIdx16, SrcIdx17, SrcIdx18, SrcIdx19;
  wire [59:0] isFullBus;

  isThisFull isthisfull_1 (.Row(Overlay_out0), .isFull(isFullBus[2:0]));
  isThisFull isthisfull_2 (.Row(Overlay_out1), .isFull(isFullBus[5:3]));
  isThisFull isthisfull_3 (.Row(Overlay_out2), .isFull(isFullBus[8:6]));
  isThisFull isthisfull_4 (.Row(Overlay_out3), .isFull(isFullBus[11:9]));
  isThisFull isthisfull_5 (.Row(Overlay_out4), .isFull(isFullBus[14:12]));
  isThisFull isthisfull_6 (.Row(Overlay_out5), .isFull(isFullBus[17:15]));
  isThisFull isthisfull_7 (.Row(Overlay_out6), .isFull(isFullBus[20:18]));
  isThisFull isthisfull_8 (.Row(Overlay_out7), .isFull(isFullBus[23:21]));
  isThisFull isthisfull_9 (.Row(Overlay_out8), .isFull(isFullBus[26:24]));
  isThisFull isthisfull_10 (.Row(Overlay_out9), .isFull(isFullBus[29:27]));
  isThisFull isthisfull_11 (.Row(Overlay_out10), .isFull(isFullBus[32:30]));
  isThisFull isthisfull_12 (.Row(Overlay_out11), .isFull(isFullBus[35:33]));
  isThisFull isthisfull_13 (.Row(Overlay_out12), .isFull(isFullBus[38:36]));
  isThisFull isthisfull_14 (.Row(Overlay_out13), .isFull(isFullBus[41:39]));
  isThisFull isthisfull_15 (.Row(Overlay_out14), .isFull(isFullBus[44:42]));
  isThisFull isthisfull_16 (.Row(Overlay_out15), .isFull(isFullBus[47:45]));
  isThisFull isthisfull_17 (.Row(Overlay_out16), .isFull(isFullBus[50:48]));
  isThisFull isthisfull_18 (.Row(Overlay_out17), .isFull(isFullBus[53:51]));
  isThisFull isthisfull_19 (.Row(Overlay_out18), .isFull(isFullBus[56:54]));
  isThisFull isthisfull_20 (.Row(Overlay_out19), .isFull(isFullBus[59:57]));
  MakingOffset makingoffset_1 (
    .isFull019(isFullBus), .Row0(offset0), .Row1(offset1), .Row2(offset2), .Row3(offset3), .Row4(offset4),
    .Row5(offset5), .Row6(offset6), .Row7(offset7), .Row8(offset8), .Row9(offset9), .Row10(offset10),
    .Row11(offset11), .Row12(offset12), .Row13(offset13), .Row14(offset14), .Row15(offset15),
    .Row16(offset16), .Row17(offset17), .Row18(offset18), .Row19(offset19));
  NewRowSelector newrowselector_1 (
    .NewRowIndex({5{1'b0}}),
    .SrcIdxBus09({SrcIdx9, SrcIdx8, SrcIdx7, SrcIdx6, SrcIdx5, SrcIdx4, SrcIdx3, SrcIdx2, SrcIdx1, SrcIdx0}),
    .SrcIdxBus1019({SrcIdx19, SrcIdx18, SrcIdx17, SrcIdx16, SrcIdx15, SrcIdx14, SrcIdx13, SrcIdx12, SrcIdx11, SrcIdx10}),
    .RowBus04({Overlay_out4, Overlay_out3, Overlay_out2, Overlay_out1, Overlay_out0}),
    .RowBus59({Overlay_out9, Overlay_out8, Overlay_out7, Overlay_out6, Overlay_out5}),
    .RowBus1014({Overlay_out14, Overlay_out13, Overlay_out12, Overlay_out11, Overlay_out10}),
    .RowBus1519({Overlay_out19, Overlay_out18, Overlay_out17, Overlay_out16, Overlay_out15}),
    .isFullBus(isFullBus), .NewRow(NewRow0));
  NewRowSelector newrowselector_2 (
    .NewRowIndex(5'b00101),
    .SrcIdxBus09({SrcIdx9, SrcIdx8, SrcIdx7, SrcIdx6, SrcIdx5, SrcIdx4, SrcIdx3, SrcIdx2, SrcIdx1, SrcIdx0}),
    .SrcIdxBus1019({SrcIdx19, SrcIdx18, SrcIdx17, SrcIdx16, SrcIdx15, SrcIdx14, SrcIdx13, SrcIdx12, SrcIdx11, SrcIdx10}),
    .RowBus04({Overlay_out4, Overlay_out3, Overlay_out2, Overlay_out1, Overlay_out0}),
    .RowBus59({Overlay_out9, Overlay_out8, Overlay_out7, Overlay_out6, Overlay_out5}),
    .RowBus1014({Overlay_out14, Overlay_out13, Overlay_out12, Overlay_out11, Overlay_out10}),
    .RowBus1519({Overlay_out19, Overlay_out18, Overlay_out17, Overlay_out16, Overlay_out15}),
    .isFullBus(isFullBus), .NewRow(NewRow5));
  NewRowSelector newrowselector_3 (
    .NewRowIndex(5'b01010),
    .SrcIdxBus09({SrcIdx9, SrcIdx8, SrcIdx7, SrcIdx6, SrcIdx5, SrcIdx4, SrcIdx3, SrcIdx2, SrcIdx1, SrcIdx0}),
    .SrcIdxBus1019({SrcIdx19, SrcIdx18, SrcIdx17, SrcIdx16, SrcIdx15, SrcIdx14, SrcIdx13, SrcIdx12, SrcIdx11, SrcIdx10}),
    .RowBus04({Overlay_out4, Overlay_out3, Overlay_out2, Overlay_out1, Overlay_out0}),
    .RowBus59({Overlay_out9, Overlay_out8, Overlay_out7, Overlay_out6, Overlay_out5}),
    .RowBus1014({Overlay_out14, Overlay_out13, Overlay_out12, Overlay_out11, Overlay_out10}),
    .RowBus1519({Overlay_out19, Overlay_out18, Overlay_out17, Overlay_out16, Overlay_out15}),
    .isFullBus(isFullBus), .NewRow(NewRow10));
  NewRowSelector newrowselector_4 (
    .NewRowIndex(5'b01111),
    .SrcIdxBus09({SrcIdx9, SrcIdx8, SrcIdx7, SrcIdx6, SrcIdx5, SrcIdx4, SrcIdx3, SrcIdx2, SrcIdx1, SrcIdx0}),
    .SrcIdxBus1019({SrcIdx19, SrcIdx18, SrcIdx17, SrcIdx16, SrcIdx15, SrcIdx14, SrcIdx13, SrcIdx12, SrcIdx11, SrcIdx10}),
    .RowBus04({Overlay_out4, Overlay_out3, Overlay_out2, Overlay_out1, Overlay_out0}),
    .RowBus59({Overlay_out9, Overlay_out8, Overlay_out7, Overlay_out6, Overlay_out5}),
    .RowBus1014({Overlay_out14, Overlay_out13, Overlay_out12, Overlay_out11, Overlay_out10}),
    .RowBus1519({Overlay_out19, Overlay_out18, Overlay_out17, Overlay_out16, Overlay_out15}),
    .isFullBus(isFullBus), .NewRow(NewRow15));
  assign bit_extender_1_out = {{2{1'b0}}, offset1};  // Bit_Extender bit_extender_1
  assign bit_extender_2_out = {{2{1'b0}}, offset2};  // Bit_Extender bit_extender_2
  assign bit_extender_3_out = {{2{1'b0}}, offset3};  // Bit_Extender bit_extender_3
  assign bit_extender_4_out = {{2{1'b0}}, offset4};  // Bit_Extender bit_extender_4
  assign bit_extender_5_out = {{2{1'b0}}, offset5};  // Bit_Extender bit_extender_5
  assign bit_extender_6_out = {{2{1'b0}}, offset6};  // Bit_Extender bit_extender_6
  assign bit_extender_7_out = {{2{1'b0}}, offset7};  // Bit_Extender bit_extender_7
  assign bit_extender_8_out = {{2{1'b0}}, offset8};  // Bit_Extender bit_extender_8
  assign bit_extender_9_out = {{2{1'b0}}, offset9};  // Bit_Extender bit_extender_9
  assign bit_extender_10_out = {{2{1'b0}}, offset10};  // Bit_Extender bit_extender_10
  assign bit_extender_11_out = {{2{1'b0}}, offset11};  // Bit_Extender bit_extender_11
  assign bit_extender_12_out = {{2{1'b0}}, offset12};  // Bit_Extender bit_extender_12
  assign bit_extender_13_out = {{2{1'b0}}, offset13};  // Bit_Extender bit_extender_13
  assign bit_extender_14_out = {{2{1'b0}}, offset14};  // Bit_Extender bit_extender_14
  assign bit_extender_15_out = {{2{1'b0}}, offset15};  // Bit_Extender bit_extender_15
  assign bit_extender_16_out = {{2{1'b0}}, offset16};  // Bit_Extender bit_extender_16
  assign bit_extender_17_out = {{2{1'b0}}, offset17};  // Bit_Extender bit_extender_17
  assign bit_extender_18_out = {{2{1'b0}}, offset18};  // Bit_Extender bit_extender_18
  assign bit_extender_19_out = {{2{1'b0}}, offset19};  // Bit_Extender bit_extender_19
  assign SrcIdx0 = {{2{1'b0}}, offset0};  // Bit_Extender bit_extender_20
  Adder #(.width(5)) adder_1 (.a(bit_extender_1_out), .b(5'b00001), .out(SrcIdx1));  // open: cin, cout
  Adder #(.width(5)) adder_2 (.a(bit_extender_2_out), .b(5'b00010), .out(SrcIdx2));  // open: cin, cout
  Adder #(.width(5)) adder_3 (.a(bit_extender_3_out), .b(5'b00011), .out(SrcIdx3));  // open: cin, cout
  Adder #(.width(5)) adder_4 (.a(bit_extender_4_out), .b(5'b00100), .out(SrcIdx4));  // open: cin, cout
  Adder #(.width(5)) adder_5 (.a(bit_extender_5_out), .b(5'b00101), .out(SrcIdx5));  // open: cin, cout
  Adder #(.width(5)) adder_6 (.a(bit_extender_6_out), .b(5'b00110), .out(SrcIdx6));  // open: cin, cout
  Adder #(.width(5)) adder_7 (.a(bit_extender_7_out), .b(5'b00111), .out(SrcIdx7));  // open: cin, cout
  Adder #(.width(5)) adder_8 (.a(bit_extender_8_out), .b(5'b01000), .out(SrcIdx8));  // open: cin, cout
  Adder #(.width(5)) adder_9 (.a(bit_extender_9_out), .b(5'b01001), .out(SrcIdx9));  // open: cin, cout
  Adder #(.width(5)) adder_10 (.a(bit_extender_10_out), .b(5'b01010), .out(SrcIdx10));  // open: cin, cout
  Adder #(.width(5)) adder_11 (.a(bit_extender_11_out), .b(5'b01011), .out(SrcIdx11));  // open: cin, cout
  Adder #(.width(5)) adder_12 (.a(bit_extender_12_out), .b(5'b01100), .out(SrcIdx12));  // open: cin, cout
  Adder #(.width(5)) adder_13 (.a(bit_extender_13_out), .b(5'b01101), .out(SrcIdx13));  // open: cin, cout
  Adder #(.width(5)) adder_14 (.a(bit_extender_14_out), .b(5'b01110), .out(SrcIdx14));  // open: cin, cout
  Adder #(.width(5)) adder_15 (.a(bit_extender_15_out), .b(5'b01111), .out(SrcIdx15));  // open: cin, cout
  Adder #(.width(5)) adder_16 (.a(bit_extender_16_out), .b(5'b10000), .out(SrcIdx16));  // open: cin, cout
  Adder #(.width(5)) adder_17 (.a(bit_extender_17_out), .b(5'b10001), .out(SrcIdx17));  // open: cin, cout
  Adder #(.width(5)) adder_18 (.a(bit_extender_18_out), .b(5'b10010), .out(SrcIdx18));  // open: cin, cout
  Adder #(.width(5)) adder_19 (.a(bit_extender_19_out), .b(5'b10011), .out(SrcIdx19));  // open: cin, cout
  NewRowSelector newrowselector_5 (
    .NewRowIndex(5'b00001),
    .SrcIdxBus09({SrcIdx9, SrcIdx8, SrcIdx7, SrcIdx6, SrcIdx5, SrcIdx4, SrcIdx3, SrcIdx2, SrcIdx1, SrcIdx0}),
    .SrcIdxBus1019({SrcIdx19, SrcIdx18, SrcIdx17, SrcIdx16, SrcIdx15, SrcIdx14, SrcIdx13, SrcIdx12, SrcIdx11, SrcIdx10}),
    .RowBus04({Overlay_out4, Overlay_out3, Overlay_out2, Overlay_out1, Overlay_out0}),
    .RowBus59({Overlay_out9, Overlay_out8, Overlay_out7, Overlay_out6, Overlay_out5}),
    .RowBus1014({Overlay_out14, Overlay_out13, Overlay_out12, Overlay_out11, Overlay_out10}),
    .RowBus1519({Overlay_out19, Overlay_out18, Overlay_out17, Overlay_out16, Overlay_out15}),
    .isFullBus(isFullBus), .NewRow(NewRow1));
  NewRowSelector newrowselector_6 (
    .NewRowIndex(5'b00110),
    .SrcIdxBus09({SrcIdx9, SrcIdx8, SrcIdx7, SrcIdx6, SrcIdx5, SrcIdx4, SrcIdx3, SrcIdx2, SrcIdx1, SrcIdx0}),
    .SrcIdxBus1019({SrcIdx19, SrcIdx18, SrcIdx17, SrcIdx16, SrcIdx15, SrcIdx14, SrcIdx13, SrcIdx12, SrcIdx11, SrcIdx10}),
    .RowBus04({Overlay_out4, Overlay_out3, Overlay_out2, Overlay_out1, Overlay_out0}),
    .RowBus59({Overlay_out9, Overlay_out8, Overlay_out7, Overlay_out6, Overlay_out5}),
    .RowBus1014({Overlay_out14, Overlay_out13, Overlay_out12, Overlay_out11, Overlay_out10}),
    .RowBus1519({Overlay_out19, Overlay_out18, Overlay_out17, Overlay_out16, Overlay_out15}),
    .isFullBus(isFullBus), .NewRow(NewRow6));
  NewRowSelector newrowselector_7 (
    .NewRowIndex(5'b01011),
    .SrcIdxBus09({SrcIdx9, SrcIdx8, SrcIdx7, SrcIdx6, SrcIdx5, SrcIdx4, SrcIdx3, SrcIdx2, SrcIdx1, SrcIdx0}),
    .SrcIdxBus1019({SrcIdx19, SrcIdx18, SrcIdx17, SrcIdx16, SrcIdx15, SrcIdx14, SrcIdx13, SrcIdx12, SrcIdx11, SrcIdx10}),
    .RowBus04({Overlay_out4, Overlay_out3, Overlay_out2, Overlay_out1, Overlay_out0}),
    .RowBus59({Overlay_out9, Overlay_out8, Overlay_out7, Overlay_out6, Overlay_out5}),
    .RowBus1014({Overlay_out14, Overlay_out13, Overlay_out12, Overlay_out11, Overlay_out10}),
    .RowBus1519({Overlay_out19, Overlay_out18, Overlay_out17, Overlay_out16, Overlay_out15}),
    .isFullBus(isFullBus), .NewRow(NewRow11));
  NewRowSelector newrowselector_8 (
    .NewRowIndex(5'b10000),
    .SrcIdxBus09({SrcIdx9, SrcIdx8, SrcIdx7, SrcIdx6, SrcIdx5, SrcIdx4, SrcIdx3, SrcIdx2, SrcIdx1, SrcIdx0}),
    .SrcIdxBus1019({SrcIdx19, SrcIdx18, SrcIdx17, SrcIdx16, SrcIdx15, SrcIdx14, SrcIdx13, SrcIdx12, SrcIdx11, SrcIdx10}),
    .RowBus04({Overlay_out4, Overlay_out3, Overlay_out2, Overlay_out1, Overlay_out0}),
    .RowBus59({Overlay_out9, Overlay_out8, Overlay_out7, Overlay_out6, Overlay_out5}),
    .RowBus1014({Overlay_out14, Overlay_out13, Overlay_out12, Overlay_out11, Overlay_out10}),
    .RowBus1519({Overlay_out19, Overlay_out18, Overlay_out17, Overlay_out16, Overlay_out15}),
    .isFullBus(isFullBus), .NewRow(NewRow16));
  Multiplexer #(.select(3), .width(4)) multiplexer_1 (
    .in0(4'b0000), .in1(4'b0010), .in2(4'b0100), .in3(4'b0110), .in4(4'b1010), .out(AddScore), .sel(offset0));  // open: in5, in6, in7
  NewRowSelector newrowselector_9 (
    .NewRowIndex(5'b00010),
    .SrcIdxBus09({SrcIdx9, SrcIdx8, SrcIdx7, SrcIdx6, SrcIdx5, SrcIdx4, SrcIdx3, SrcIdx2, SrcIdx1, SrcIdx0}),
    .SrcIdxBus1019({SrcIdx19, SrcIdx18, SrcIdx17, SrcIdx16, SrcIdx15, SrcIdx14, SrcIdx13, SrcIdx12, SrcIdx11, SrcIdx10}),
    .RowBus04({Overlay_out4, Overlay_out3, Overlay_out2, Overlay_out1, Overlay_out0}),
    .RowBus59({Overlay_out9, Overlay_out8, Overlay_out7, Overlay_out6, Overlay_out5}),
    .RowBus1014({Overlay_out14, Overlay_out13, Overlay_out12, Overlay_out11, Overlay_out10}),
    .RowBus1519({Overlay_out19, Overlay_out18, Overlay_out17, Overlay_out16, Overlay_out15}),
    .isFullBus(isFullBus), .NewRow(NewRow2));
  NewRowSelector newrowselector_10 (
    .NewRowIndex(5'b00111),
    .SrcIdxBus09({SrcIdx9, SrcIdx8, SrcIdx7, SrcIdx6, SrcIdx5, SrcIdx4, SrcIdx3, SrcIdx2, SrcIdx1, SrcIdx0}),
    .SrcIdxBus1019({SrcIdx19, SrcIdx18, SrcIdx17, SrcIdx16, SrcIdx15, SrcIdx14, SrcIdx13, SrcIdx12, SrcIdx11, SrcIdx10}),
    .RowBus04({Overlay_out4, Overlay_out3, Overlay_out2, Overlay_out1, Overlay_out0}),
    .RowBus59({Overlay_out9, Overlay_out8, Overlay_out7, Overlay_out6, Overlay_out5}),
    .RowBus1014({Overlay_out14, Overlay_out13, Overlay_out12, Overlay_out11, Overlay_out10}),
    .RowBus1519({Overlay_out19, Overlay_out18, Overlay_out17, Overlay_out16, Overlay_out15}),
    .isFullBus(isFullBus), .NewRow(NewRow7));
  NewRowSelector newrowselector_11 (
    .NewRowIndex(5'b01100),
    .SrcIdxBus09({SrcIdx9, SrcIdx8, SrcIdx7, SrcIdx6, SrcIdx5, SrcIdx4, SrcIdx3, SrcIdx2, SrcIdx1, SrcIdx0}),
    .SrcIdxBus1019({SrcIdx19, SrcIdx18, SrcIdx17, SrcIdx16, SrcIdx15, SrcIdx14, SrcIdx13, SrcIdx12, SrcIdx11, SrcIdx10}),
    .RowBus04({Overlay_out4, Overlay_out3, Overlay_out2, Overlay_out1, Overlay_out0}),
    .RowBus59({Overlay_out9, Overlay_out8, Overlay_out7, Overlay_out6, Overlay_out5}),
    .RowBus1014({Overlay_out14, Overlay_out13, Overlay_out12, Overlay_out11, Overlay_out10}),
    .RowBus1519({Overlay_out19, Overlay_out18, Overlay_out17, Overlay_out16, Overlay_out15}),
    .isFullBus(isFullBus), .NewRow(NewRow12));
  NewRowSelector newrowselector_12 (
    .NewRowIndex(5'b10001),
    .SrcIdxBus09({SrcIdx9, SrcIdx8, SrcIdx7, SrcIdx6, SrcIdx5, SrcIdx4, SrcIdx3, SrcIdx2, SrcIdx1, SrcIdx0}),
    .SrcIdxBus1019({SrcIdx19, SrcIdx18, SrcIdx17, SrcIdx16, SrcIdx15, SrcIdx14, SrcIdx13, SrcIdx12, SrcIdx11, SrcIdx10}),
    .RowBus04({Overlay_out4, Overlay_out3, Overlay_out2, Overlay_out1, Overlay_out0}),
    .RowBus59({Overlay_out9, Overlay_out8, Overlay_out7, Overlay_out6, Overlay_out5}),
    .RowBus1014({Overlay_out14, Overlay_out13, Overlay_out12, Overlay_out11, Overlay_out10}),
    .RowBus1519({Overlay_out19, Overlay_out18, Overlay_out17, Overlay_out16, Overlay_out15}),
    .isFullBus(isFullBus), .NewRow(NewRow17));
  NewRowSelector newrowselector_13 (
    .NewRowIndex(5'b00011),
    .SrcIdxBus09({SrcIdx9, SrcIdx8, SrcIdx7, SrcIdx6, SrcIdx5, SrcIdx4, SrcIdx3, SrcIdx2, SrcIdx1, SrcIdx0}),
    .SrcIdxBus1019({SrcIdx19, SrcIdx18, SrcIdx17, SrcIdx16, SrcIdx15, SrcIdx14, SrcIdx13, SrcIdx12, SrcIdx11, SrcIdx10}),
    .RowBus04({Overlay_out4, Overlay_out3, Overlay_out2, Overlay_out1, Overlay_out0}),
    .RowBus59({Overlay_out9, Overlay_out8, Overlay_out7, Overlay_out6, Overlay_out5}),
    .RowBus1014({Overlay_out14, Overlay_out13, Overlay_out12, Overlay_out11, Overlay_out10}),
    .RowBus1519({Overlay_out19, Overlay_out18, Overlay_out17, Overlay_out16, Overlay_out15}),
    .isFullBus(isFullBus), .NewRow(NewRow3));
  NewRowSelector newrowselector_14 (
    .NewRowIndex(5'b01000),
    .SrcIdxBus09({SrcIdx9, SrcIdx8, SrcIdx7, SrcIdx6, SrcIdx5, SrcIdx4, SrcIdx3, SrcIdx2, SrcIdx1, SrcIdx0}),
    .SrcIdxBus1019({SrcIdx19, SrcIdx18, SrcIdx17, SrcIdx16, SrcIdx15, SrcIdx14, SrcIdx13, SrcIdx12, SrcIdx11, SrcIdx10}),
    .RowBus04({Overlay_out4, Overlay_out3, Overlay_out2, Overlay_out1, Overlay_out0}),
    .RowBus59({Overlay_out9, Overlay_out8, Overlay_out7, Overlay_out6, Overlay_out5}),
    .RowBus1014({Overlay_out14, Overlay_out13, Overlay_out12, Overlay_out11, Overlay_out10}),
    .RowBus1519({Overlay_out19, Overlay_out18, Overlay_out17, Overlay_out16, Overlay_out15}),
    .isFullBus(isFullBus), .NewRow(NewRow8));
  NewRowSelector newrowselector_15 (
    .NewRowIndex(5'b01101),
    .SrcIdxBus09({SrcIdx9, SrcIdx8, SrcIdx7, SrcIdx6, SrcIdx5, SrcIdx4, SrcIdx3, SrcIdx2, SrcIdx1, SrcIdx0}),
    .SrcIdxBus1019({SrcIdx19, SrcIdx18, SrcIdx17, SrcIdx16, SrcIdx15, SrcIdx14, SrcIdx13, SrcIdx12, SrcIdx11, SrcIdx10}),
    .RowBus04({Overlay_out4, Overlay_out3, Overlay_out2, Overlay_out1, Overlay_out0}),
    .RowBus59({Overlay_out9, Overlay_out8, Overlay_out7, Overlay_out6, Overlay_out5}),
    .RowBus1014({Overlay_out14, Overlay_out13, Overlay_out12, Overlay_out11, Overlay_out10}),
    .RowBus1519({Overlay_out19, Overlay_out18, Overlay_out17, Overlay_out16, Overlay_out15}),
    .isFullBus(isFullBus), .NewRow(NewRow13));
  NewRowSelector newrowselector_16 (
    .NewRowIndex(5'b10010),
    .SrcIdxBus09({SrcIdx9, SrcIdx8, SrcIdx7, SrcIdx6, SrcIdx5, SrcIdx4, SrcIdx3, SrcIdx2, SrcIdx1, SrcIdx0}),
    .SrcIdxBus1019({SrcIdx19, SrcIdx18, SrcIdx17, SrcIdx16, SrcIdx15, SrcIdx14, SrcIdx13, SrcIdx12, SrcIdx11, SrcIdx10}),
    .RowBus04({Overlay_out4, Overlay_out3, Overlay_out2, Overlay_out1, Overlay_out0}),
    .RowBus59({Overlay_out9, Overlay_out8, Overlay_out7, Overlay_out6, Overlay_out5}),
    .RowBus1014({Overlay_out14, Overlay_out13, Overlay_out12, Overlay_out11, Overlay_out10}),
    .RowBus1519({Overlay_out19, Overlay_out18, Overlay_out17, Overlay_out16, Overlay_out15}),
    .isFullBus(isFullBus), .NewRow(NewRow18));
  NewRowSelector newrowselector_17 (
    .NewRowIndex(5'b00100),
    .SrcIdxBus09({SrcIdx9, SrcIdx8, SrcIdx7, SrcIdx6, SrcIdx5, SrcIdx4, SrcIdx3, SrcIdx2, SrcIdx1, SrcIdx0}),
    .SrcIdxBus1019({SrcIdx19, SrcIdx18, SrcIdx17, SrcIdx16, SrcIdx15, SrcIdx14, SrcIdx13, SrcIdx12, SrcIdx11, SrcIdx10}),
    .RowBus04({Overlay_out4, Overlay_out3, Overlay_out2, Overlay_out1, Overlay_out0}),
    .RowBus59({Overlay_out9, Overlay_out8, Overlay_out7, Overlay_out6, Overlay_out5}),
    .RowBus1014({Overlay_out14, Overlay_out13, Overlay_out12, Overlay_out11, Overlay_out10}),
    .RowBus1519({Overlay_out19, Overlay_out18, Overlay_out17, Overlay_out16, Overlay_out15}),
    .isFullBus(isFullBus), .NewRow(NewRow4));
  NewRowSelector newrowselector_18 (
    .NewRowIndex(5'b01001),
    .SrcIdxBus09({SrcIdx9, SrcIdx8, SrcIdx7, SrcIdx6, SrcIdx5, SrcIdx4, SrcIdx3, SrcIdx2, SrcIdx1, SrcIdx0}),
    .SrcIdxBus1019({SrcIdx19, SrcIdx18, SrcIdx17, SrcIdx16, SrcIdx15, SrcIdx14, SrcIdx13, SrcIdx12, SrcIdx11, SrcIdx10}),
    .RowBus04({Overlay_out4, Overlay_out3, Overlay_out2, Overlay_out1, Overlay_out0}),
    .RowBus59({Overlay_out9, Overlay_out8, Overlay_out7, Overlay_out6, Overlay_out5}),
    .RowBus1014({Overlay_out14, Overlay_out13, Overlay_out12, Overlay_out11, Overlay_out10}),
    .RowBus1519({Overlay_out19, Overlay_out18, Overlay_out17, Overlay_out16, Overlay_out15}),
    .isFullBus(isFullBus), .NewRow(NewRow9));
  NewRowSelector newrowselector_19 (
    .NewRowIndex(5'b01110),
    .SrcIdxBus09({SrcIdx9, SrcIdx8, SrcIdx7, SrcIdx6, SrcIdx5, SrcIdx4, SrcIdx3, SrcIdx2, SrcIdx1, SrcIdx0}),
    .SrcIdxBus1019({SrcIdx19, SrcIdx18, SrcIdx17, SrcIdx16, SrcIdx15, SrcIdx14, SrcIdx13, SrcIdx12, SrcIdx11, SrcIdx10}),
    .RowBus04({Overlay_out4, Overlay_out3, Overlay_out2, Overlay_out1, Overlay_out0}),
    .RowBus59({Overlay_out9, Overlay_out8, Overlay_out7, Overlay_out6, Overlay_out5}),
    .RowBus1014({Overlay_out14, Overlay_out13, Overlay_out12, Overlay_out11, Overlay_out10}),
    .RowBus1519({Overlay_out19, Overlay_out18, Overlay_out17, Overlay_out16, Overlay_out15}),
    .isFullBus(isFullBus), .NewRow(NewRow14));
  NewRowSelector newrowselector_20 (
    .NewRowIndex(5'b10011),
    .SrcIdxBus09({SrcIdx9, SrcIdx8, SrcIdx7, SrcIdx6, SrcIdx5, SrcIdx4, SrcIdx3, SrcIdx2, SrcIdx1, SrcIdx0}),
    .SrcIdxBus1019({SrcIdx19, SrcIdx18, SrcIdx17, SrcIdx16, SrcIdx15, SrcIdx14, SrcIdx13, SrcIdx12, SrcIdx11, SrcIdx10}),
    .RowBus04({Overlay_out4, Overlay_out3, Overlay_out2, Overlay_out1, Overlay_out0}),
    .RowBus59({Overlay_out9, Overlay_out8, Overlay_out7, Overlay_out6, Overlay_out5}),
    .RowBus1014({Overlay_out14, Overlay_out13, Overlay_out12, Overlay_out11, Overlay_out10}),
    .RowBus1519({Overlay_out19, Overlay_out18, Overlay_out17, Overlay_out16, Overlay_out15}),
    .isFullBus(isFullBus), .NewRow(NewRow19));

  // Other names for the same wires on the sheet: isFullRow0[2:0] = isFullBus[2:0]; isFullRow1[2:0] = isFullBus[5:3];
  //   isFullRow2[2:0] = isFullBus[8:6]; isFullRow3[2:0] = isFullBus[11:9]; isFullRow4[2:0] = isFullBus[14:12];
  //   isFullRow5[2:0] = isFullBus[17:15]; isFullRow6[2:0] = isFullBus[20:18]; isFullRow7[2:0] = isFullBus[23:21];
  //   isFullRow8[2:0] = isFullBus[26:24]; isFullRow9[2:0] = isFullBus[29:27]; isFullRow10[2:0] = isFullBus[32:30];
  //   isFullRow11[2:0] = isFullBus[35:33]; isFullRow12[2:0] = isFullBus[38:36]; isFullRow13[2:0] = isFullBus[41:39];
  //   isFullRow14[2:0] = isFullBus[44:42]; isFullRow15[2:0] = isFullBus[47:45]; isFullRow16[2:0] = isFullBus[50:48];
  //   isFullRow17[2:0] = isFullBus[53:51]; isFullRow18[2:0] = isFullBus[56:54]; isFullRow19[2:0] = isFullBus[59:57];
  //   Row0[9:0] = Overlay_out0;
  //   Rowbus04[49:0] = {Overlay_out4, Overlay_out3, Overlay_out2, Overlay_out1, Overlay_out0};
  //   Row1[9:0] = Overlay_out1; Row2[9:0] = Overlay_out2; Row3[9:0] = Overlay_out3; Row4[9:0] = Overlay_out4;
  //   Row5[9:0] = Overlay_out5;
  //   Rowbus59[49:0] = {Overlay_out9, Overlay_out8, Overlay_out7, Overlay_out6, Overlay_out5};
  //   Row6[9:0] = Overlay_out6; Row7[9:0] = Overlay_out7; Row8[9:0] = Overlay_out8; Row9[9:0] = Overlay_out9;
  //   Row10[9:0] = Overlay_out10;
  //   Rowbus1014[49:0] = {Overlay_out14, Overlay_out13, Overlay_out12, Overlay_out11, Overlay_out10};
  //   Row11[9:0] = Overlay_out11; Row12[9:0] = Overlay_out12; Row13[9:0] = Overlay_out13; Row14[9:0] = Overlay_out14;
  //   Row15[9:0] = Overlay_out15;
  //   Rowbus1519[49:0] = {Overlay_out19, Overlay_out18, Overlay_out17, Overlay_out16, Overlay_out15};
  //   Row16[9:0] = Overlay_out16; Row17[9:0] = Overlay_out17; Row18[9:0] = Overlay_out18; Row19[9:0] = Overlay_out19;
  //   SrcIdxBus09[49:0] = {SrcIdx9, SrcIdx8, SrcIdx7, SrcIdx6, SrcIdx5, SrcIdx4, SrcIdx3, SrcIdx2, SrcIdx1, SrcIdx0};
  //   SrcIdxBus1019[49:0] = {SrcIdx19, SrcIdx18, SrcIdx17, SrcIdx16, SrcIdx15, SrcIdx14, SrcIdx13, SrcIdx12, SrcIdx11, SrcIdx10}
endmodule

module isThisFull (
  input  [9:0] Row,
  output [2:0] isFull
);

  wire and_1_out;

  assign isFull = {{2{1'b0}}, and_1_out};  // Bit_Extender bit_extender_1
  and and_1 (and_1_out, Row[0], Row[1], Row[2], Row[3], Row[4], Row[5], Row[6], Row[7], Row[8], Row[9]);
endmodule

module MakingOffset (
  input  [59:0] isFull019,
  output [2:0] Row0,
  output [2:0] Row1,
  output [2:0] Row2,
  output [2:0] Row3,
  output [2:0] Row4,
  output [2:0] Row5,
  output [2:0] Row6,
  output [2:0] Row7,
  output [2:0] Row8,
  output [2:0] Row9,
  output [2:0] Row10,
  output [2:0] Row11,
  output [2:0] Row12,
  output [2:0] Row13,
  output [2:0] Row14,
  output [2:0] Row15,
  output [2:0] Row16,
  output [2:0] Row17,
  output [2:0] Row18,
  output [2:0] Row19
);

  Adder #(.width(3)) adder_1 (.a(3'b000), .b(isFull019[59:57]), .out(Row18));  // open: cin, cout
  Adder #(.width(3)) adder_2 (.a(Row18), .b(isFull019[56:54]), .out(Row17));  // open: cin, cout
  Adder #(.width(3)) adder_3 (.a(Row17), .b(isFull019[53:51]), .out(Row16));  // open: cin, cout
  Adder #(.width(3)) adder_4 (.a(Row16), .b(isFull019[50:48]), .out(Row15));  // open: cin, cout
  Adder #(.width(3)) adder_5 (.a(Row15), .b(isFull019[47:45]), .out(Row14));  // open: cin, cout
  Adder #(.width(3)) adder_6 (.a(Row14), .b(isFull019[44:42]), .out(Row13));  // open: cin, cout
  Adder #(.width(3)) adder_7 (.a(Row13), .b(isFull019[41:39]), .out(Row12));  // open: cin, cout
  Adder #(.width(3)) adder_8 (.a(Row12), .b(isFull019[38:36]), .out(Row11));  // open: cin, cout
  Adder #(.width(3)) adder_9 (.a(Row11), .b(isFull019[35:33]), .out(Row10));  // open: cin, cout
  Adder #(.width(3)) adder_10 (.a(Row10), .b(isFull019[32:30]), .out(Row9));  // open: cin, cout
  Adder #(.width(3)) adder_11 (.a(Row9), .b(isFull019[29:27]), .out(Row8));  // open: cin, cout
  Adder #(.width(3)) adder_12 (.a(Row8), .b(isFull019[26:24]), .out(Row7));  // open: cin, cout
  Adder #(.width(3)) adder_13 (.a(Row7), .b(isFull019[23:21]), .out(Row6));  // open: cin, cout
  Adder #(.width(3)) adder_14 (.a(Row6), .b(isFull019[20:18]), .out(Row5));  // open: cin, cout
  Adder #(.width(3)) adder_15 (.a(Row5), .b(isFull019[17:15]), .out(Row4));  // open: cin, cout
  Adder #(.width(3)) adder_16 (.a(Row4), .b(isFull019[14:12]), .out(Row3));  // open: cin, cout
  Adder #(.width(3)) adder_17 (.a(Row3), .b(isFull019[11:9]), .out(Row2));  // open: cin, cout
  Adder #(.width(3)) adder_18 (.a(Row2), .b(isFull019[8:6]), .out(Row1));  // open: cin, cout
  Adder #(.width(3)) adder_19 (.a(Row1), .b(isFull019[5:3]), .out(Row0));  // open: cin, cout
  Adder #(.width(3)) adder_20 (.a(Row0));  // open: b, out, cin, cout

  assign Row19 = 3'b000;

  // Other names for the same wires on the sheet: isFullRow0[2:0] = isFull019[2:0]; isFullRow1[2:0] = isFull019[5:3];
  //   isFullRow2[2:0] = isFull019[8:6]; isFullRow3[2:0] = isFull019[11:9]; isFullRow4[2:0] = isFull019[14:12];
  //   isFullRow5[2:0] = isFull019[17:15]; isFullRow6[2:0] = isFull019[20:18]; isFullRow7[2:0] = isFull019[23:21];
  //   isFullRow8[2:0] = isFull019[26:24]; isFullRow9[2:0] = isFull019[29:27]; isFullRow10[2:0] = isFull019[32:30];
  //   isFullRow11[2:0] = isFull019[35:33]; isFullRow12[2:0] = isFull019[38:36]; isFullRow13[2:0] = isFull019[41:39];
  //   isFullRow14[2:0] = isFull019[44:42]; isFullRow15[2:0] = isFull019[47:45]; isFullRow16[2:0] = isFull019[50:48];
  //   isFullRow17[2:0] = isFull019[53:51]; isFullRow18[2:0] = isFull019[56:54]; isFullRow19[2:0] = isFull019[59:57];
  //   offset0[2:0] = Row0; offset1[2:0] = Row1; offset2[2:0] = Row2; offset3[2:0] = Row3; offset4[2:0] = Row4;
  //   offset5[2:0] = Row5; offset6[2:0] = Row6; offset7[2:0] = Row7; offset8[2:0] = Row8; offset9[2:0] = Row9;
  //   offset10[2:0] = Row10; offset11[2:0] = Row11; offset12[2:0] = Row12; offset13[2:0] = Row13;
  //   offset14[2:0] = Row14; offset15[2:0] = Row15; offset16[2:0] = Row16; offset17[2:0] = Row17;
  //   offset18[2:0] = Row18
endmodule

module NewRowSelector (
  input  [4:0] NewRowIndex,
  input  [49:0] SrcIdxBus09,
  input  [49:0] SrcIdxBus1019,
  input  [49:0] RowBus04,
  input  [49:0] RowBus59,
  input  [49:0] RowBus1014,
  input  [49:0] RowBus1519,
  input  [59:0] isFullBus,
  output [9:0] NewRow
);

  wire and_1_out, and_2_out, and_3_out, and_4_out, and_5_out, and_6_out, and_7_out, and_8_out, and_9_out,
       and_10_out, and_11_out, and_12_out, and_13_out, and_14_out, and_15_out, and_16_out, and_17_out,
       and_18_out, and_19_out, and_20_out, comparator_1_eq, comparator_2_eq, comparator_3_eq,
       comparator_4_eq, comparator_5_eq, comparator_6_eq, comparator_7_eq, comparator_8_eq, comparator_9_eq,
       comparator_10_eq, comparator_11_eq, comparator_12_eq, comparator_13_eq, comparator_14_eq,
       comparator_15_eq, comparator_16_eq, comparator_17_eq, comparator_18_eq, comparator_19_eq,
       comparator_20_eq, isFullRow0, isFullRow1, isFullRow2, isFullRow3, isFullRow4, isFullRow5, isFullRow6,
       isFullRow7, isFullRow8, isFullRow9, isFullRow10, isFullRow11, isFullRow12, isFullRow13, isFullRow14,
       isFullRow15, isFullRow16, isFullRow17, isFullRow18, isFullRow19;
  wire [9:0] and_21_out, and_22_out, and_23_out, and_24_out, and_25_out, and_26_out, and_27_out, and_28_out,
       and_29_out, and_30_out, and_31_out, and_32_out, and_33_out, and_34_out, and_35_out, and_36_out,
       and_37_out, and_38_out, and_39_out, and_40_out, bit_extender_1_out, bit_extender_2_out,
       bit_extender_3_out, bit_extender_4_out, bit_extender_5_out, bit_extender_6_out, bit_extender_7_out,
       bit_extender_8_out, bit_extender_9_out, bit_extender_10_out, bit_extender_11_out, bit_extender_12_out,
       bit_extender_13_out, bit_extender_14_out, bit_extender_15_out, bit_extender_16_out,
       bit_extender_17_out, bit_extender_18_out, bit_extender_19_out, bit_extender_20_out;

  not not_1 (isFullRow0, isFullBus[0]);
  not not_2 (isFullRow1, isFullBus[3]);
  not not_3 (isFullRow2, isFullBus[6]);
  not not_4 (isFullRow3, isFullBus[9]);
  not not_5 (isFullRow4, isFullBus[12]);
  not not_6 (isFullRow5, isFullBus[15]);
  not not_7 (isFullRow6, isFullBus[18]);
  not not_8 (isFullRow7, isFullBus[21]);
  not not_9 (isFullRow8, isFullBus[24]);
  not not_10 (isFullRow9, isFullBus[27]);
  not not_11 (isFullRow10, isFullBus[30]);
  not not_12 (isFullRow11, isFullBus[33]);
  not not_13 (isFullRow12, isFullBus[36]);
  not not_14 (isFullRow13, isFullBus[39]);
  not not_15 (isFullRow14, isFullBus[42]);
  not not_16 (isFullRow15, isFullBus[45]);
  not not_17 (isFullRow16, isFullBus[48]);
  not not_18 (isFullRow17, isFullBus[51]);
  not not_19 (isFullRow18, isFullBus[54]);
  not not_20 (isFullRow19, isFullBus[57]);
  Comparator #(.mode("unsigned"), .width(5)) comparator_1 (
    .a(SrcIdxBus09[4:0]), .b(NewRowIndex), .eq(comparator_1_eq));  // open: gt, lt
  Comparator #(.mode("unsigned"), .width(5)) comparator_2 (
    .a(SrcIdxBus09[9:5]), .b(NewRowIndex), .eq(comparator_2_eq));  // open: gt, lt
  Comparator #(.mode("unsigned"), .width(5)) comparator_3 (
    .a(SrcIdxBus09[14:10]), .b(NewRowIndex), .eq(comparator_3_eq));  // open: gt, lt
  Comparator #(.mode("unsigned"), .width(5)) comparator_4 (
    .a(SrcIdxBus09[19:15]), .b(NewRowIndex), .eq(comparator_4_eq));  // open: gt, lt
  Comparator #(.mode("unsigned"), .width(5)) comparator_5 (
    .a(SrcIdxBus09[24:20]), .b(NewRowIndex), .eq(comparator_5_eq));  // open: gt, lt
  Comparator #(.mode("unsigned"), .width(5)) comparator_6 (
    .a(SrcIdxBus09[29:25]), .b(NewRowIndex), .eq(comparator_6_eq));  // open: gt, lt
  Comparator #(.mode("unsigned"), .width(5)) comparator_7 (
    .a(SrcIdxBus09[34:30]), .b(NewRowIndex), .eq(comparator_7_eq));  // open: gt, lt
  Comparator #(.mode("unsigned"), .width(5)) comparator_8 (
    .a(SrcIdxBus09[39:35]), .b(NewRowIndex), .eq(comparator_8_eq));  // open: gt, lt
  Comparator #(.mode("unsigned"), .width(5)) comparator_9 (
    .a(SrcIdxBus09[44:40]), .b(NewRowIndex), .eq(comparator_9_eq));  // open: gt, lt
  Comparator #(.mode("unsigned"), .width(5)) comparator_10 (
    .a(SrcIdxBus09[49:45]), .b(NewRowIndex), .eq(comparator_10_eq));  // open: gt, lt
  Comparator #(.mode("unsigned"), .width(5)) comparator_11 (
    .a(SrcIdxBus1019[4:0]), .b(NewRowIndex), .eq(comparator_11_eq));  // open: gt, lt
  Comparator #(.mode("unsigned"), .width(5)) comparator_12 (
    .a(SrcIdxBus1019[9:5]), .b(NewRowIndex), .eq(comparator_12_eq));  // open: gt, lt
  Comparator #(.mode("unsigned"), .width(5)) comparator_13 (
    .a(SrcIdxBus1019[14:10]), .b(NewRowIndex), .eq(comparator_13_eq));  // open: gt, lt
  Comparator #(.mode("unsigned"), .width(5)) comparator_14 (
    .a(SrcIdxBus1019[19:15]), .b(NewRowIndex), .eq(comparator_14_eq));  // open: gt, lt
  Comparator #(.mode("unsigned"), .width(5)) comparator_15 (
    .a(SrcIdxBus1019[24:20]), .b(NewRowIndex), .eq(comparator_15_eq));  // open: gt, lt
  Comparator #(.mode("unsigned"), .width(5)) comparator_16 (
    .a(SrcIdxBus1019[29:25]), .b(NewRowIndex), .eq(comparator_16_eq));  // open: gt, lt
  Comparator #(.mode("unsigned"), .width(5)) comparator_17 (
    .a(SrcIdxBus1019[34:30]), .b(NewRowIndex), .eq(comparator_17_eq));  // open: gt, lt
  Comparator #(.mode("unsigned"), .width(5)) comparator_18 (
    .a(SrcIdxBus1019[39:35]), .b(NewRowIndex), .eq(comparator_18_eq));  // open: gt, lt
  Comparator #(.mode("unsigned"), .width(5)) comparator_19 (
    .a(SrcIdxBus1019[44:40]), .b(NewRowIndex), .eq(comparator_19_eq));  // open: gt, lt
  Comparator #(.mode("unsigned"), .width(5)) comparator_20 (
    .a(SrcIdxBus1019[49:45]), .b(NewRowIndex), .eq(comparator_20_eq));  // open: gt, lt
  assign bit_extender_1_out = {{9{and_1_out}}, and_1_out};  // Bit_Extender bit_extender_1
  and and_1 (and_1_out, isFullRow0, comparator_1_eq);
  assign bit_extender_2_out = {{9{and_2_out}}, and_2_out};  // Bit_Extender bit_extender_2
  and and_2 (and_2_out, isFullRow1, comparator_2_eq);
  assign bit_extender_3_out = {{9{and_3_out}}, and_3_out};  // Bit_Extender bit_extender_3
  and and_3 (and_3_out, isFullRow2, comparator_3_eq);
  assign bit_extender_4_out = {{9{and_4_out}}, and_4_out};  // Bit_Extender bit_extender_4
  and and_4 (and_4_out, isFullRow3, comparator_4_eq);
  assign bit_extender_5_out = {{9{and_5_out}}, and_5_out};  // Bit_Extender bit_extender_5
  and and_5 (and_5_out, isFullRow4, comparator_5_eq);
  assign bit_extender_6_out = {{9{and_6_out}}, and_6_out};  // Bit_Extender bit_extender_6
  and and_6 (and_6_out, isFullRow5, comparator_6_eq);
  assign bit_extender_7_out = {{9{and_7_out}}, and_7_out};  // Bit_Extender bit_extender_7
  and and_7 (and_7_out, isFullRow6, comparator_7_eq);
  assign bit_extender_8_out = {{9{and_8_out}}, and_8_out};  // Bit_Extender bit_extender_8
  and and_8 (and_8_out, isFullRow7, comparator_8_eq);
  assign bit_extender_9_out = {{9{and_9_out}}, and_9_out};  // Bit_Extender bit_extender_9
  and and_9 (and_9_out, isFullRow8, comparator_9_eq);
  assign bit_extender_10_out = {{9{and_10_out}}, and_10_out};  // Bit_Extender bit_extender_10
  and and_10 (and_10_out, isFullRow9, comparator_10_eq);
  assign bit_extender_11_out = {{9{and_11_out}}, and_11_out};  // Bit_Extender bit_extender_11
  and and_11 (and_11_out, isFullRow10, comparator_11_eq);
  assign bit_extender_12_out = {{9{and_12_out}}, and_12_out};  // Bit_Extender bit_extender_12
  and and_12 (and_12_out, isFullRow11, comparator_12_eq);
  assign bit_extender_13_out = {{9{and_13_out}}, and_13_out};  // Bit_Extender bit_extender_13
  and and_13 (and_13_out, isFullRow12, comparator_13_eq);
  assign bit_extender_14_out = {{9{and_14_out}}, and_14_out};  // Bit_Extender bit_extender_14
  and and_14 (and_14_out, isFullRow13, comparator_14_eq);
  assign bit_extender_15_out = {{9{and_15_out}}, and_15_out};  // Bit_Extender bit_extender_15
  and and_15 (and_15_out, isFullRow14, comparator_15_eq);
  assign bit_extender_16_out = {{9{and_16_out}}, and_16_out};  // Bit_Extender bit_extender_16
  and and_16 (and_16_out, isFullRow15, comparator_16_eq);
  assign bit_extender_17_out = {{9{and_17_out}}, and_17_out};  // Bit_Extender bit_extender_17
  and and_17 (and_17_out, isFullRow16, comparator_17_eq);
  assign bit_extender_18_out = {{9{and_18_out}}, and_18_out};  // Bit_Extender bit_extender_18
  and and_18 (and_18_out, isFullRow17, comparator_18_eq);
  assign bit_extender_19_out = {{9{and_19_out}}, and_19_out};  // Bit_Extender bit_extender_19
  and and_19 (and_19_out, isFullRow18, comparator_19_eq);
  assign bit_extender_20_out = {{9{and_20_out}}, and_20_out};  // Bit_Extender bit_extender_20
  and and_20 (and_20_out, isFullRow19, comparator_20_eq);
  assign and_21_out = RowBus04[9:0] & bit_extender_1_out;  // AND_Gate and_21, 10 bits wide
  assign and_22_out = RowBus04[19:10] & bit_extender_2_out;  // AND_Gate and_22, 10 bits wide
  assign and_23_out = RowBus04[29:20] & bit_extender_3_out;  // AND_Gate and_23, 10 bits wide
  assign and_24_out = RowBus04[39:30] & bit_extender_4_out;  // AND_Gate and_24, 10 bits wide
  assign and_25_out = RowBus04[49:40] & bit_extender_5_out;  // AND_Gate and_25, 10 bits wide
  assign and_26_out = RowBus59[9:0] & bit_extender_6_out;  // AND_Gate and_26, 10 bits wide
  assign and_27_out = RowBus59[19:10] & bit_extender_7_out;  // AND_Gate and_27, 10 bits wide
  assign and_28_out = RowBus59[29:20] & bit_extender_8_out;  // AND_Gate and_28, 10 bits wide
  assign and_29_out = RowBus59[39:30] & bit_extender_9_out;  // AND_Gate and_29, 10 bits wide
  assign and_30_out = RowBus59[49:40] & bit_extender_10_out;  // AND_Gate and_30, 10 bits wide
  assign and_31_out = RowBus1014[9:0] & bit_extender_11_out;  // AND_Gate and_31, 10 bits wide
  assign and_32_out = RowBus1014[19:10] & bit_extender_12_out;  // AND_Gate and_32, 10 bits wide
  assign and_33_out = RowBus1014[29:20] & bit_extender_13_out;  // AND_Gate and_33, 10 bits wide
  assign and_34_out = RowBus1014[39:30] & bit_extender_14_out;  // AND_Gate and_34, 10 bits wide
  assign and_35_out = RowBus1014[49:40] & bit_extender_15_out;  // AND_Gate and_35, 10 bits wide
  assign and_36_out = RowBus1519[9:0] & bit_extender_16_out;  // AND_Gate and_36, 10 bits wide
  assign and_37_out = RowBus1519[19:10] & bit_extender_17_out;  // AND_Gate and_37, 10 bits wide
  assign and_38_out = RowBus1519[29:20] & bit_extender_18_out;  // AND_Gate and_38, 10 bits wide
  assign and_39_out = RowBus1519[39:30] & bit_extender_19_out;  // AND_Gate and_39, 10 bits wide
  assign and_40_out = RowBus1519[49:40] & bit_extender_20_out;  // AND_Gate and_40, 10 bits wide
  assign NewRow = and_21_out | and_22_out | and_23_out | and_24_out | and_25_out | and_26_out | and_27_out | and_28_out | and_29_out | and_30_out | and_31_out | and_32_out | and_33_out | and_34_out | and_35_out | and_36_out | and_37_out | and_38_out | and_39_out | and_40_out;  // OR_Gate or_1, 10 bits wide

  // Other names for the same wires on the sheet: Row0[9:0] = RowBus04[9:0]; Row1[9:0] = RowBus04[19:10];
  //   Row2[9:0] = RowBus04[29:20]; Row3[9:0] = RowBus04[39:30]; Row4[9:0] = RowBus04[49:40];
  //   Row5[9:0] = RowBus59[9:0]; Row6[9:0] = RowBus59[19:10]; Row7[9:0] = RowBus59[29:20];
  //   Row8[9:0] = RowBus59[39:30]; Row9[9:0] = RowBus59[49:40]; Row10[9:0] = RowBus1014[9:0];
  //   Row11[9:0] = RowBus1014[19:10]; Row12[9:0] = RowBus1014[29:20]; Row13[9:0] = RowBus1014[39:30];
  //   Row14[9:0] = RowBus1014[49:40]; Row15[9:0] = RowBus1519[9:0]; Row16[9:0] = RowBus1519[19:10];
  //   Row17[9:0] = RowBus1519[29:20]; Row18[9:0] = RowBus1519[39:30]; Row19[9:0] = RowBus1519[49:40];
  //   SrcIdx0[4:0] = SrcIdxBus09[4:0]; SrcIdx1[4:0] = SrcIdxBus09[9:5]; SrcIdx2[4:0] = SrcIdxBus09[14:10];
  //   SrcIdx3[4:0] = SrcIdxBus09[19:15]; SrcIdx4[4:0] = SrcIdxBus09[24:20]; SrcIdx5[4:0] = SrcIdxBus09[29:25];
  //   SrcIdx6[4:0] = SrcIdxBus09[34:30]; SrcIdx7[4:0] = SrcIdxBus09[39:35]; SrcIdx8[4:0] = SrcIdxBus09[44:40];
  //   SrcIdx9[4:0] = SrcIdxBus09[49:45]; SrcIdx10[4:0] = SrcIdxBus1019[4:0]; SrcIdx11[4:0] = SrcIdxBus1019[9:5];
  //   SrcIdx12[4:0] = SrcIdxBus1019[14:10]; SrcIdx13[4:0] = SrcIdxBus1019[19:15];
  //   SrcIdx14[4:0] = SrcIdxBus1019[24:20]; SrcIdx15[4:0] = SrcIdxBus1019[29:25];
  //   SrcIdx16[4:0] = SrcIdxBus1019[34:30]; SrcIdx17[4:0] = SrcIdxBus1019[39:35];
  //   SrcIdx18[4:0] = SrcIdxBus1019[44:40]; SrcIdx19[4:0] = SrcIdxBus1019[49:45]
endmodule

module Score_Level (
  input  [3:0] AddScore,
  input  Lock,
  output [6:0] Score,
  output [3:0] Seg_1,
  output [3:0] Seg_10,
  output [3:0] LV,
  output Clear
);

  wire and_1_out, and_2_out, and_3_out, and_4_out, comparator_1_lt, comparator_2_lt, comparator_3_lt,
       comparator_4_lt, comparator_6_gt, not_1_out, not_2_out, not_3_out, not_4_out, not_5_out, not_6_out,
       not_7_out, not_8_out;
  wire [6:0] adder_1_out, bit_extender_1_out, multiplexer_1_out;
  wire [6:4] divider_1_out, divider_1_rem;

  assign bit_extender_1_out = {{3{1'b0}}, AddScore};  // Bit_Extender bit_extender_1
  Adder #(.width(7)) adder_1 (.a(Score), .b(bit_extender_1_out), .out(adder_1_out));  // open: cin, cout
  Comparator #(.mode("unsigned"), .width(7)) comparator_1 (
    .a(Score), .b(7'b0001010), .lt(comparator_1_lt));  // open: gt, eq
  Comparator #(.mode("unsigned"), .width(7)) comparator_2 (
    .a(Score), .b(7'b0011110), .lt(comparator_2_lt));  // open: gt, eq
  Comparator #(.mode("unsigned"), .width(7)) comparator_3 (
    .a(Score), .b(7'b0110010), .lt(comparator_3_lt));  // open: gt, eq
  Comparator #(.mode("unsigned"), .width(7)) comparator_4 (
    .a(Score), .b(7'b1011010), .lt(comparator_4_lt));  // open: gt, eq
  Comparator #(.mode("unsigned"), .width(7)) comparator_5 (.a(Score), .b(7'b1100011), .eq(Clear));  // open: gt, lt
  Comparator #(.mode("unsigned"), .width(7)) comparator_6 (
    .a(adder_1_out), .b(7'b1100011), .gt(comparator_6_gt));  // open: eq, lt
  not not_1 (not_1_out, comparator_1_lt);
  and and_1 (and_1_out, not_1_out, not_2_out);
  not not_2 (not_2_out, not_3_out);
  not not_3 (not_3_out, comparator_2_lt);
  not not_4 (not_4_out, not_5_out);
  not not_5 (not_5_out, comparator_3_lt);
  not not_6 (not_6_out, not_7_out);
  not not_7 (not_7_out, comparator_4_lt);
  Register #(.width(7)) register_1 (.D(multiplexer_1_out), .en(1'b1), .clk(Lock), .Q(Score));  // open: clr
  Multiplexer #(.width(7)) multiplexer_1 (
    .in0(adder_1_out), .in1(7'b1100011), .out(multiplexer_1_out), .sel(comparator_6_gt));
  and and_2 (and_2_out, not_3_out, not_4_out);
  and and_3 (and_3_out, not_5_out, not_6_out);
  and and_4 (and_4_out, not_7_out, not_8_out);
  not not_8 (not_8_out, Clear);
  Priority_Encoder #(.select(4)) priority_encoder_1 (
    .in0(comparator_1_lt), .in1(and_1_out), .in2(and_2_out), .in3(and_3_out), .in4(and_4_out), .in5(Clear),
    .out(LV));  // open: in6, in7, in8, in9, in10, in11, in12, in13, in14, in15, gs, en_out, en_in
  Divider #(.width(7)) divider_1 (
    .a(Score), .b(7'b0001010), .out({divider_1_out, Seg_1}), .upper({7{1'b0}}), .rem({divider_1_rem, Seg_10}));
endmodule
